// Logisim project computer.circ as structural Verilog: 19 circuits, main circuit main
module main (
);

  wire and_1_out, and_2_out, clock_1_out, comparator_1_eq, comparator_2_eq, Reset_out, SOC_memload,
       SOC_memstore;
  wire [3:0] SOC_membyteselect;
  wire [31:0] PC, RAM_ADDRESS, RAM_OUT, SOC_memdatawrite;

  Comparator #(.width(32)) comparator_1 (.a(PC), .b(RAM_ADDRESS), .eq(comparator_1_eq));  // open: gt, lt
  Comparator #(.width(32)) comparator_2 (.a(RAM_OUT), .b({32{1'b0}}), .eq(comparator_2_eq));  // open: gt, lt
  // Probe on PC
  and and_1 (and_1_out, comparator_1_eq, comparator_2_eq);
  and and_2 (and_2_out, ~and_1_out, clock_1_out);  // AND_Gate
  Clock clock_1 (.out(clock_1_out));
  SOC SOC (
    .memDataRead(RAM_OUT), .memAddress(RAM_ADDRESS), .memDataWrite(SOC_memdatawrite),
    .memByteSelect(SOC_membyteselect), .memStore(SOC_memstore), .memLoad(SOC_memload), .programCounter(PC),
    .CLK(and_2_out), .RESET(Reset_out));
  Button Reset (.out(Reset_out));
  MainMemory RAM (
    .addressIn(RAM_ADDRESS), .dataOut(RAM_OUT), .dataIn(SOC_memdatawrite), .store(SOC_memstore),
    .load(SOC_memload), .clk(and_2_out), .byteSelect(SOC_membyteselect));  // open: reset
endmodule

module Adder (
  input  [31:0] aOperand,
  input  [31:0] bOperand,
  input  subtract,
  output [31:0] result
);

  wire [31:0] adder_1_out, subtractor_1_out;

  Adder_part #(.width(32)) adder_1 (.a(aOperand), .b(bOperand), .out(adder_1_out), .cin(1'b0));  // open: cout
  Subtractor #(.width(32)) subtractor_1 (.a(aOperand), .b(bOperand), .out(subtractor_1_out), .bin(1'b0));  // open: bout
  Multiplexer #(.width(32), .enable("false")) multiplexer_1 (
    .in0(adder_1_out), .in1(subtractor_1_out), .out(result), .sel(subtract));

  // Notes on the sheet:
  //   This circuit performs A+B
  //   This circuit performs A-B
  //   MUX used to switch which result we output, + or -
endmodule

module Divider (
  input  [31:0] aOperand,
  input  [31:0] bOperand,
  input  unsignedEn,
  output [31:0] divResult,
  output [31:0] remResult
);

  wire a_isNegative, b_isNegative, xor_1_out;
  wire [31:0] AbsVal_2_absoluteval, AbsVal_absoluteval, divider_1_out, divider_1_rem;

  AbsoluteValue AbsVal (
    .IN(aOperand), .Unsigned(unsignedEn), .AbsoluteVal(AbsVal_absoluteval), .NegativeInput(a_isNegative));
  AbsoluteValue AbsVal_2 (
    .IN(bOperand), .Unsigned(unsignedEn), .AbsoluteVal(AbsVal_2_absoluteval), .NegativeInput(b_isNegative));
  Divider_part #(.width(32)) divider_1 (
    .a(AbsVal_absoluteval), .b(AbsVal_2_absoluteval), .out(divider_1_out), .rem(divider_1_rem));  // open: upper
  xor xor_1 (xor_1_out, a_isNegative, b_isNegative);
  FlipSign FlipSign (.flip(xor_1_out), .operand(divider_1_out), .result(divResult));
  FlipSign FlipSign_2 (.flip(a_isNegative), .operand(divider_1_rem), .result(remResult));

  // Notes on the sheet:
  //   Performs A/B
  //   Take absolute value of inputs
  //   Make result negative if inputs had opposite signs
  //   Make remainder negative if quotient (A) was negative
endmodule

module Pipeline (
  input  [31:0] memoryDataRead,
  input  clk,
  input  reset,
  output [31:0] programCounter_out,
  output [31:0] memoryAddress,
  output [31:0] memoryDataWrite,
  output [1:0] memoryLength,
  output store,
  output load,
  output loadUnsigned
);

  wire and_1_out, and_2_out, and_4_out, auipc_frameOut, auipcInst_decode, branchInst_decode,
       branchInst_frameOut, compareEquals, compareGreater, compareLess, decodeState, executeState,
       fetch_ReceiveState, fetch_RequestState, immediateSelect_decodeOut, immediateSelect_frameOut,
       jumpLink_decode, jumpLink_frameOut, jumpRegister_decode, jumpRegister_frameOut, load_decode,
       load_frameOut, loadUnsigned_decode, memReadState, or_1_out, or_2_out, or_3_out, setupState,
       store_decode, store_frameOut, subtractEnable_decodeOut, subtractEnable_frameOut,
       unsignedSelect_decodeOut, unsignedSelect_frameOut, writebackState, writeEnable_decodeOut,
       writeEnable_frameOut;
  wire [0:0] or_4_out;
  wire [1:0] memLength_decode, memLength_frameOut;
  wire [2:0] branchType_decode, branchType_frameOut, resultSelect_decodeOut, resultSelect_frameOut;
  wire [4:0] a_location_decodeOut, aLoc_frameOut, b_location_decodeOut, bLoc_frameOut, writeSelect_decodeOut,
       writeSelect_frameOut;
  wire [31:0] adderOut, aluResult, aOpCompare_frameIn, aOpCompare_frameOut, aOperand_frameOut,
       aOperand_muxOut, bOpCompare_frameOut, bOpCompare_muxOut, bOperand_frameOut, bOperand_muxOut,
       divideOut, immediateVal_decodeOut, immediateVal_frameOut, instructionFetchController_instructionout,
       mulOut, multiplexer_4_out, programCounter_next, readB_regOut, remOut;

  // Probe on memoryDataRead
  PipelineStateController StateController (
    .loadInst(load_frameOut), .clk(clk), .reset(reset), .fetch_RequestState(fetch_RequestState),
    .fetch_ReceiveState(fetch_ReceiveState), .decodeState(decodeState), .setupState(setupState),
    .executeState(executeState), .memReadState(memReadState), .writebackState(writebackState));
  Multiplexer #(.width(32), .enable("false")) multiplexer_1 (
    .in0(readB_regOut), .in1(immediateVal_frameOut), .out(bOperand_muxOut), .sel(immediateSelect_frameOut));
  and and_1 (and_1_out, ~branchInst_frameOut, immediateSelect_frameOut);  // AND_Gate
  Multiplexer #(.width(32), .enable("false")) multiplexer_2 (
    .in0(readB_regOut), .in1(immediateVal_frameOut), .out(bOpCompare_muxOut), .sel(and_1_out));
  or or_1 (or_1_out, jumpLink_frameOut, jumpRegister_frameOut);
  // Probe on instructionFetchController_instructionout
  instructionFetchController instructionFetchController (
    .memoryIn(memoryDataRead), .cir_writeEnable(fetch_ReceiveState), .pcOverwrite(aluResult),
    .pc_writeEnable(executeState), .branchType(branchType_frameOut), .jumpInst(or_1_out),
    .compareGreater(compareGreater), .compareEquals(compareEquals), .compareLess(compareLess), .clk(clk),
    .reset(reset), .instructionOut(instructionFetchController_instructionout),
    .programCounter(programCounter_out), .programCounter_next(programCounter_next));
  InstructionFrame instructionframe_1 (
    .aOperand_in(aOperand_muxOut), .aLoc_in(a_location_decodeOut), .bOperand_in(bOperand_muxOut),
    .bLoc_in(b_location_decodeOut), .immediateVal_in(immediateVal_decodeOut),
    .immediateSelect_in(immediateSelect_decodeOut), .unsignedSelect_in(unsignedSelect_decodeOut),
    .subtractEnable_in(subtractEnable_decodeOut), .resultSelect_in(resultSelect_decodeOut),
    .writeSelect_in(writeSelect_decodeOut), .writeEnable_in(writeEnable_decodeOut),
    .branchInst_in(branchInst_decode), .branchType_in(branchType_decode), .jumpLink_in(jumpLink_decode),
    .jumpRegister_in(jumpRegister_decode), .aOpCompare_in(aOpCompare_frameIn),
    .bOpCompare_in(bOpCompare_muxOut), .load_In(load_decode), .loadUnsigned_In(loadUnsigned_decode),
    .store_In(store_decode), .memLength_In(memLength_decode), .storeData_in(readB_regOut),
    .auipc_In(auipcInst_decode), .writebackState(writebackState), .memReadState(memReadState),
    .executeState(executeState), .setupState(setupState), .decodeState(decodeState),
    .fetch_ReceiveState(fetch_ReceiveState), .fetch_RequestState(fetch_RequestState), .clk(clk),
    .reset(reset), .aOperand_out(aOperand_frameOut), .aLoc_out(aLoc_frameOut),
    .bOperand_out(bOperand_frameOut), .bLoc_out(bLoc_frameOut), .immediateVal_out(immediateVal_frameOut),
    .immediateSelect_out(immediateSelect_frameOut), .unsignedSelect_out(unsignedSelect_frameOut),
    .subtractEnable_out(subtractEnable_frameOut), .ResultSelect_Out(resultSelect_frameOut),
    .WriteSelect_Out(writeSelect_frameOut), .WriteEnable_Out(writeEnable_frameOut),
    .branchInst_out(branchInst_frameOut), .branchType_Out(branchType_frameOut),
    .jumpLInk_Out(jumpLink_frameOut), .jumpRegister_Out(jumpRegister_frameOut),
    .AOpCompare_Out(aOpCompare_frameOut), .BOpCompare_Out(bOpCompare_frameOut), .load_Out(load_frameOut),
    .loadUnsigned_Out(loadUnsigned), .store_Out(store_frameOut), .memLength_Out(memLength_frameOut),
    .storeData_Out(memoryDataWrite), .auipc_Out(auipc_frameOut));
  InstructionDecoder instructiondecoder_1 (
    .instructionIn(instructionFetchController_instructionout), .A_Location(a_location_decodeOut),
    .B_Location(b_location_decodeOut), .ImmediateSelect(immediateSelect_decodeOut),
    .Immediate(immediateVal_decodeOut), .Unsigned(unsignedSelect_decodeOut),
    .SubtractEnable(subtractEnable_decodeOut), .writeSelect(writeSelect_decodeOut),
    .writeEnable(writeEnable_decodeOut), .resultSelect(resultSelect_decodeOut),
    .branchInst(branchInst_decode), .branchType(branchType_decode), .jumpLink(jumpLink_decode),
    .jumpRegister(jumpRegister_decode), .load(load_decode), .loadUnsigned(loadUnsigned_decode),
    .store(store_decode), .memLength(memLength_decode), .auipcInst(auipcInst_decode));  // open: error
  or or_2 (or_2_out, auipc_frameOut, jumpLink_frameOut, branchInst_frameOut);
  Multiplexer #(.width(32), .enable("false")) multiplexer_3 (
    .in0(aOpCompare_frameIn), .in1(programCounter_out), .out(aOperand_muxOut), .sel(or_2_out));
  or or_3 (or_3_out, executeState, memReadState);
  Adder Adder (
    .aOperand(aOperand_frameOut), .bOperand(bOperand_frameOut), .subtract(subtractEnable_frameOut),
    .result(adderOut));
  Multiplier Multiplier (.aOperand(aOperand_frameOut), .bOperand(bOperand_frameOut), .result(mulOut));
  Divider Divider (
    .aOperand(aOperand_frameOut), .bOperand(bOperand_frameOut), .unsignedEn(unsignedSelect_frameOut),
    .divResult(divideOut), .remResult(remOut));
  Compare Compare (
    .aOperand(aOpCompare_frameOut), .bOperand(bOpCompare_frameOut), .unsignedEn(unsignedSelect_frameOut),
    .greater(compareGreater), .equal(compareEquals), .less(compareLess));
  or or_4 (or_4_out[0], jumpRegister_frameOut, jumpLink_frameOut);
  and and_2 (and_2_out, or_3_out, writeEnable_frameOut);
  Multiplexer #(.select(2), .width(32), .enable("false")) multiplexer_4 (
    .in0(aluResult), .in1(programCounter_next), .in2(memoryDataRead), .out(multiplexer_4_out),
    .sel({load_frameOut, or_4_out[0]}));  // open: in3
  Registers registers_1 (
    .dataIn(multiplexer_4_out), .writeSelect(writeSelect_frameOut), .writeEnable(and_2_out),
    .readA_Select(aLoc_frameOut), .readB_Select(bLoc_frameOut), .clock(clk), .reset(reset),
    .readA_out(aOpCompare_frameIn), .readB_out(readB_regOut));
  Multiplexer #(.select(3), .width(32), .enable("false")) multiplexer_5 (
    .in0(adderOut), .in1(mulOut), .in2(divideOut), .in3(remOut), .in4({{31{1'b0}}, compareGreater}),
    .in5({{31{1'b0}}, compareEquals}), .in6({{31{1'b0}}, compareLess}), .out(aluResult),
    .sel(resultSelect_frameOut));  // open: in7
  Multiplexer #(.width(32), .enable("false")) multiplexer_6 (
    .in0(aluResult), .in1(programCounter_out), .out(memoryAddress), .sel(writebackState));
  Multiplexer #(.width(2), .enable("false")) multiplexer_7 (
    .in0(memLength_frameOut), .in1(2'b11), .out(memoryLength), .sel(writebackState));
  and and_3 (store, store_frameOut, executeState);
  and and_4 (and_4_out, load_frameOut, executeState);
  or or_5 (load, and_4_out, writebackState);

  // Other names for the same wires on the sheet: equalsOut[0] = compareEquals; greaterThanOut[0] = compareGreater;
  //   lessThanOut[0] = compareLess; loadUnsigned_frameOut = loadUnsigned; programCounter[31:0] = programCounter_out;
  //   readA_regOut[31:0] = aOpCompare_frameIn; storeData_frameIn[31:0] = readB_regOut;
  //   storeData_frameOut[31:0] = memoryDataWrite

  // Notes on the sheet:
  //   Input Pin Connections
  //   Control state of pipeline
  //   Control writes to all pipeline memory
  //   Store operands and control signals in an instruction frame
  //   Decode instruction and generate control signals
  //   Arithmetic execution units
  //   Pad comparison results with 0s so that result is 32 bits
  //   General purpose registers
  //   Output Pin Connections
  //   .
endmodule

module Compare (
  input  [31:0] aOperand,
  input  [31:0] bOperand,
  input  unsignedEn,
  output greater,
  output equal,
  output less
);

  wire comp_Greater, comp_Less, dontFlipOutputs, nor_1_out;

  Comparator #(.width(32), .mode("unsigned")) comparator_1 (
    .a(aOperand), .b(bOperand), .gt(comp_Greater), .eq(equal), .lt(comp_Less));
  or or_1 (dontFlipOutputs, unsignedEn, nor_1_out);
  nor nor_1 (nor_1_out, aOperand[31], bOperand[31]);
  Multiplexer #(.enable("false")) multiplexer_1 (
    .in0(comp_Less), .in1(comp_Greater), .out(greater), .sel(dontFlipOutputs));
  Multiplexer #(.enable("false")) multiplexer_2 (
    .in0(comp_Greater), .in1(comp_Less), .out(less), .sel(dontFlipOutputs));

  // Other names for the same wires on the sheet: a_isNegative = aOperand[31]; b_isNegative = bOperand[31];
  //   comp_Equals = equal

  // Notes on the sheet:
  //   Inputs
  //   Outputs
endmodule

module Registers (
  input  [31:0] dataIn,
  input  [4:0] writeSelect,
  input  writeEnable,
  input  [4:0] readA_Select,
  input  [4:0] readB_Select,
  input  clock,
  input  reset,
  output [31:0] readA_out,
  output [31:0] readB_out
);

  wire and_1_out, and_2_out, and_3_out, and_4_out, and_5_out, and_6_out, and_7_out, and_8_out, and_9_out,
       and_10_out, and_11_out, and_12_out, and_13_out, and_14_out, and_15_out, and_16_out, and_17_out,
       and_18_out, and_19_out, and_20_out, and_21_out, and_22_out, and_23_out, and_24_out, and_25_out,
       and_26_out, and_27_out, and_28_out, and_29_out, and_30_out, and_31_out, r0_select, r1_select,
       r2_select, r3_select, r4_select, r5_select, r6_select, r7_select, r8_select, r9_select, r10_select,
       r11_select, r12_select, r13_select, r14_select, r15_select, r16_select, r17_select, r18_select,
       r19_select, r20_select, r21_select, r22_select, r23_select, r24_select, r25_select, r26_select,
       r27_select, r28_select, r29_select, r30_select, r31_select;
  wire [31:0] r1_dataOut, r2_dataOut, r3_dataOut, r4_dataOut, r5_dataOut, r6_dataOut, r7_dataOut, r8_dataOut,
       r9_dataOut, r10_dataOut, r11_dataOut, r12_dataOut, r13_dataOut, r14_dataOut, r15_dataOut, r16_dataOut,
       r17_dataOut, r18_dataOut, r19_dataOut, r20_dataOut, r21_dataOut, r22_dataOut, r23_dataOut,
       r24_dataOut, r25_dataOut, r26_dataOut, r27_dataOut, r28_dataOut, r29_dataOut, r30_dataOut, r31_dataOut;

  // Probe on {32{1'b0}}
  // Probe on r1_dataOut
  // Probe on r2_dataOut
  // Probe on r3_dataOut
  // Probe on r4_dataOut
  // Probe on r5_dataOut
  // Probe on r6_dataOut
  // Probe on r7_dataOut
  // Probe on r8_dataOut
  // Probe on r9_dataOut
  // Probe on r10_dataOut
  // Probe on r11_dataOut
  // Probe on r12_dataOut
  // Probe on r13_dataOut
  // Probe on r14_dataOut
  // Probe on r15_dataOut
  // Probe on r16_dataOut
  // Probe on r17_dataOut
  // Probe on r18_dataOut
  // Probe on r19_dataOut
  // Probe on r20_dataOut
  // Probe on r21_dataOut
  // Probe on r22_dataOut
  // Probe on r23_dataOut
  // Probe on r24_dataOut
  // Probe on r25_dataOut
  // Probe on r26_dataOut
  // Probe on r27_dataOut
  // Probe on r28_dataOut
  // Probe on r29_dataOut
  // Probe on r30_dataOut
  // Probe on r31_dataOut
  // Probe on {32{1'b0}}
  // Probe on r1_dataOut
  // Probe on r2_dataOut
  // Probe on r3_dataOut
  // Probe on r4_dataOut
  // Probe on r5_dataOut
  // Probe on r6_dataOut
  // Probe on r7_dataOut
  // Probe on r8_dataOut
  // Probe on r9_dataOut
  // Probe on r10_dataOut
  // Probe on r11_dataOut
  // Probe on r12_dataOut
  // Probe on r13_dataOut
  // Probe on r14_dataOut
  // Probe on r15_dataOut
  // Probe on r16_dataOut
  // Probe on r17_dataOut
  // Probe on r18_dataOut
  // Probe on r19_dataOut
  // Probe on r20_dataOut
  // Probe on r21_dataOut
  // Probe on r22_dataOut
  // Probe on r23_dataOut
  // Probe on r24_dataOut
  // Probe on r25_dataOut
  // Probe on r26_dataOut
  // Probe on r27_dataOut
  // Probe on r28_dataOut
  // Probe on r29_dataOut
  // Probe on r30_dataOut
  // Probe on r31_dataOut
  Decoder #(.select(5), .enable("false")) decoder_1 (
    .out0(r0_select), .out1(r1_select), .out2(r2_select), .out3(r3_select), .out4(r4_select),
    .out5(r5_select), .out6(r6_select), .out7(r7_select), .out8(r8_select), .out9(r9_select),
    .out10(r10_select), .out11(r11_select), .out12(r12_select), .out13(r13_select), .out14(r14_select),
    .out15(r15_select), .out16(r16_select), .out17(r17_select), .out18(r18_select), .out19(r19_select),
    .out20(r20_select), .out21(r21_select), .out22(r22_select), .out23(r23_select), .out24(r24_select),
    .out25(r25_select), .out26(r26_select), .out27(r27_select), .out28(r28_select), .out29(r29_select),
    .out30(r30_select), .out31(r31_select), .sel(writeSelect));
  and and_1 (and_1_out, r1_select, writeEnable);
  and and_2 (and_2_out, r2_select, writeEnable);
  and and_3 (and_3_out, r3_select, writeEnable);
  and and_4 (and_4_out, r4_select, writeEnable);
  and and_5 (and_5_out, r5_select, writeEnable);
  and and_6 (and_6_out, r6_select, writeEnable);
  and and_7 (and_7_out, r7_select, writeEnable);
  and and_8 (and_8_out, r8_select, writeEnable);
  and and_9 (and_9_out, r9_select, writeEnable);
  and and_10 (and_10_out, r10_select, writeEnable);
  and and_11 (and_11_out, r11_select, writeEnable);
  and and_12 (and_12_out, r12_select, writeEnable);
  and and_13 (and_13_out, r13_select, writeEnable);
  and and_14 (and_14_out, r14_select, writeEnable);
  and and_15 (and_15_out, r15_select, writeEnable);
  and and_16 (and_16_out, r16_select, writeEnable);
  and and_17 (and_17_out, r17_select, writeEnable);
  and and_18 (and_18_out, r18_select, writeEnable);
  and and_19 (and_19_out, r19_select, writeEnable);
  and and_20 (and_20_out, r20_select, writeEnable);
  and and_21 (and_21_out, r21_select, writeEnable);
  and and_22 (and_22_out, r22_select, writeEnable);
  and and_23 (and_23_out, r23_select, writeEnable);
  and and_24 (and_24_out, r24_select, writeEnable);
  and and_25 (and_25_out, r25_select, writeEnable);
  and and_26 (and_26_out, r26_select, writeEnable);
  and and_27 (and_27_out, r27_select, writeEnable);
  and and_28 (and_28_out, r28_select, writeEnable);
  and and_29 (and_29_out, r29_select, writeEnable);
  and and_30 (and_30_out, r30_select, writeEnable);
  and and_31 (and_31_out, r31_select, writeEnable);
  Register #(.width(32)) r1 (.D(dataIn), .en(and_1_out), .Q(r1_dataOut), .clk(clock), .clr(reset));
  Register #(.width(32)) r2 (.D(dataIn), .en(and_2_out), .Q(r2_dataOut), .clk(clock), .clr(reset));
  Register #(.width(32)) r3 (.D(dataIn), .en(and_3_out), .Q(r3_dataOut), .clk(clock), .clr(reset));
  Register #(.width(32)) r4 (.D(dataIn), .en(and_4_out), .Q(r4_dataOut), .clk(clock), .clr(reset));
  Register #(.width(32)) r5 (.D(dataIn), .en(and_5_out), .Q(r5_dataOut), .clk(clock), .clr(reset));
  Register #(.width(32)) r6 (.D(dataIn), .en(and_6_out), .Q(r6_dataOut), .clk(clock), .clr(reset));
  Register #(.width(32)) r7 (.D(dataIn), .en(and_7_out), .Q(r7_dataOut), .clk(clock), .clr(reset));
  Register #(.width(32)) r8 (.D(dataIn), .en(and_8_out), .Q(r8_dataOut), .clk(clock), .clr(reset));
  Register #(.width(32)) r9 (.D(dataIn), .en(and_9_out), .Q(r9_dataOut), .clk(clock), .clr(reset));
  Register #(.width(32)) r10 (.D(dataIn), .en(and_10_out), .Q(r10_dataOut), .clk(clock), .clr(reset));
  Register #(.width(32)) r11 (.D(dataIn), .en(and_11_out), .Q(r11_dataOut), .clk(clock), .clr(reset));
  Register #(.width(32)) r12 (.D(dataIn), .en(and_12_out), .Q(r12_dataOut), .clk(clock), .clr(reset));
  Register #(.width(32)) r13 (.D(dataIn), .en(and_13_out), .Q(r13_dataOut), .clk(clock), .clr(reset));
  Register #(.width(32)) r14 (.D(dataIn), .en(and_14_out), .Q(r14_dataOut), .clk(clock), .clr(reset));
  Register #(.width(32)) r15 (.D(dataIn), .en(and_15_out), .Q(r15_dataOut), .clk(clock), .clr(reset));
  Register #(.width(32)) r16 (.D(dataIn), .en(and_16_out), .Q(r16_dataOut), .clk(clock), .clr(reset));
  Register #(.width(32)) r17 (.D(dataIn), .en(and_17_out), .Q(r17_dataOut), .clk(clock), .clr(reset));
  Register #(.width(32)) r18 (.D(dataIn), .en(and_18_out), .Q(r18_dataOut), .clk(clock), .clr(reset));
  Register #(.width(32)) r19 (.D(dataIn), .en(and_19_out), .Q(r19_dataOut), .clk(clock), .clr(reset));
  Register #(.width(32)) r20 (.D(dataIn), .en(and_20_out), .Q(r20_dataOut), .clk(clock), .clr(reset));
  Register #(.width(32)) r21 (.D(dataIn), .en(and_21_out), .Q(r21_dataOut), .clk(clock), .clr(reset));
  Register #(.width(32)) r22 (.D(dataIn), .en(and_22_out), .Q(r22_dataOut), .clk(clock), .clr(reset));
  Register #(.width(32)) r23 (.D(dataIn), .en(and_23_out), .Q(r23_dataOut), .clk(clock), .clr(reset));
  Register #(.width(32)) r24 (.D(dataIn), .en(and_24_out), .Q(r24_dataOut), .clk(clock), .clr(reset));
  Register #(.width(32)) r25 (.D(dataIn), .en(and_25_out), .Q(r25_dataOut), .clk(clock), .clr(reset));
  Register #(.width(32)) r26 (.D(dataIn), .en(and_26_out), .Q(r26_dataOut), .clk(clock), .clr(reset));
  Register #(.width(32)) r27 (.D(dataIn), .en(and_27_out), .Q(r27_dataOut), .clk(clock), .clr(reset));
  Register #(.width(32)) r28 (.D(dataIn), .en(and_28_out), .Q(r28_dataOut), .clk(clock), .clr(reset));
  Register #(.width(32)) r29 (.D(dataIn), .en(and_29_out), .Q(r29_dataOut), .clk(clock), .clr(reset));
  Register #(.width(32)) r30 (.D(dataIn), .en(and_30_out), .Q(r30_dataOut), .clk(clock), .clr(reset));
  Register #(.width(32)) r31 (.D(dataIn), .en(and_31_out), .Q(r31_dataOut), .clk(clock), .clr(reset));
  Multiplexer #(.select(5), .width(32), .enable("false")) multiplexer_1 (
    .in0({32{1'b0}}), .in1(r1_dataOut), .in2(r2_dataOut), .in3(r3_dataOut), .in4(r4_dataOut),
    .in5(r5_dataOut), .in6(r6_dataOut), .in7(r7_dataOut), .in8(r8_dataOut), .in9(r9_dataOut),
    .in10(r10_dataOut), .in11(r11_dataOut), .in12(r12_dataOut), .in13(r13_dataOut), .in14(r14_dataOut),
    .in15(r15_dataOut), .in16(r16_dataOut), .in17(r17_dataOut), .in18(r18_dataOut), .in19(r19_dataOut),
    .in20(r20_dataOut), .in21(r21_dataOut), .in22(r22_dataOut), .in23(r23_dataOut), .in24(r24_dataOut),
    .in25(r25_dataOut), .in26(r26_dataOut), .in27(r27_dataOut), .in28(r28_dataOut), .in29(r29_dataOut),
    .in30(r30_dataOut), .in31(r31_dataOut), .out(readB_out), .sel(readB_Select));
  Multiplexer #(.select(5), .width(32), .enable("false")) multiplexer_2 (
    .in0({32{1'b0}}), .in1(r1_dataOut), .in2(r2_dataOut), .in3(r3_dataOut), .in4(r4_dataOut),
    .in5(r5_dataOut), .in6(r6_dataOut), .in7(r7_dataOut), .in8(r8_dataOut), .in9(r9_dataOut),
    .in10(r10_dataOut), .in11(r11_dataOut), .in12(r12_dataOut), .in13(r13_dataOut), .in14(r14_dataOut),
    .in15(r15_dataOut), .in16(r16_dataOut), .in17(r17_dataOut), .in18(r18_dataOut), .in19(r19_dataOut),
    .in20(r20_dataOut), .in21(r21_dataOut), .in22(r22_dataOut), .in23(r23_dataOut), .in24(r24_dataOut),
    .in25(r25_dataOut), .in26(r26_dataOut), .in27(r27_dataOut), .in28(r28_dataOut), .in29(r29_dataOut),
    .in30(r30_dataOut), .in31(r31_dataOut), .out(readA_out), .sel(readA_Select));

  // Notes on the sheet:
  //   Input Pins
  //   Register Probes
  //   Signed
  //   Unsigned
  //   zero
  //   ra
  //   sp
  //   gp
  //   tp
  //   t0
  //   t1
  //   t2
  //   s0/fp
  //   s1
  //   a0
  //   a1
  //   a2
  //   a3
  //   a4
  //   a5
  //   a6
  //   a7
  //   s2
  //   s3
  //   s4
  //   s5
  //   s6
  //   s7
  //   s8
  //   s9
  //   s10
  //   s11
  //   t3
  //   t4
  //   t5
  //   t6
  //   This decodes the write select input, and determines which register gets written to
  //   Our bank of 32 registers
  //   x0 (register 0) is hardwired to 0 in the RISCV spec (section 2.1)
  //   These muxes determine which register values to output based on read select value
endmodule

module Multiplier (
  input  [31:0] aOperand,
  input  [31:0] bOperand,
  output [31:0] result
);

  Multiplier_part #(.width(32)) multiplier_1 (
    .a(aOperand), .b(bOperand), .out(result), .cin({32{1'b0}}));  // open: cout

  // Notes on the sheet:
  //   AxB
endmodule

module AbsoluteValue (
  input  Unsigned,
  input  [31:0] IN,
  output [31:0] AbsoluteVal,
  output NegativeInput
);

  wire not_1_out;

  not not_1 (not_1_out, Unsigned);
  and and_1 (NegativeInput, not_1_out, IN[31]);
  FlipSign FlipSign (.flip(NegativeInput), .operand(IN), .result(AbsoluteVal));

  // Other names for the same wires on the sheet: isNegative = NegativeInput

  // Notes on the sheet:
  //   This circuit takes the absolue value of the input, and outputs if the input was negative
  //   Flip sign if input is negative
  //   <- If the MSB is 1, then the incoming number must be negative
  //   Output absolute value, and sign of the input
endmodule

module FlipSign (
  input  flip,
  input  [31:0] operand,
  output [31:0] result
);

  wire [31:0] xor_1_out;

  xor xor_1 (xor_1_out[0], flip, operand[0]);
  xor xor_2 (xor_1_out[1], flip, operand[1]);
  xor xor_3 (xor_1_out[2], flip, operand[2]);
  xor xor_4 (xor_1_out[3], flip, operand[3]);
  xor xor_5 (xor_1_out[4], flip, operand[4]);
  xor xor_6 (xor_1_out[5], flip, operand[5]);
  xor xor_7 (xor_1_out[6], flip, operand[6]);
  xor xor_8 (xor_1_out[7], flip, operand[7]);
  xor xor_9 (xor_1_out[8], flip, operand[8]);
  xor xor_10 (xor_1_out[9], flip, operand[9]);
  xor xor_11 (xor_1_out[10], flip, operand[10]);
  xor xor_12 (xor_1_out[11], flip, operand[11]);
  xor xor_13 (xor_1_out[12], flip, operand[12]);
  xor xor_14 (xor_1_out[13], flip, operand[13]);
  xor xor_15 (xor_1_out[14], flip, operand[14]);
  xor xor_16 (xor_1_out[15], flip, operand[15]);
  xor xor_17 (xor_1_out[16], flip, operand[16]);
  xor xor_18 (xor_1_out[17], flip, operand[17]);
  xor xor_19 (xor_1_out[18], flip, operand[18]);
  xor xor_20 (xor_1_out[19], flip, operand[19]);
  xor xor_21 (xor_1_out[20], flip, operand[20]);
  xor xor_22 (xor_1_out[21], flip, operand[21]);
  xor xor_23 (xor_1_out[22], flip, operand[22]);
  xor xor_24 (xor_1_out[23], flip, operand[23]);
  xor xor_25 (xor_1_out[24], flip, operand[24]);
  xor xor_26 (xor_1_out[25], flip, operand[25]);
  xor xor_27 (xor_1_out[26], flip, operand[26]);
  xor xor_28 (xor_1_out[27], flip, operand[27]);
  xor xor_29 (xor_1_out[28], flip, operand[28]);
  xor xor_30 (xor_1_out[29], flip, operand[29]);
  xor xor_31 (xor_1_out[30], flip, operand[30]);
  xor xor_32 (xor_1_out[31], flip, operand[31]);
  Adder_part #(.width(32)) adder_1 (.a(xor_1_out), .b({32{1'b0}}), .out(result), .cin(flip));  // open: cout

  // Other names for the same wires on the sheet: b0 = operand[0]; b1 = operand[1]; b2 = operand[2]; b3 = operand[3];
  //   b4 = operand[4]; b5 = operand[5]; b6 = operand[6]; b7 = operand[7]; b8 = operand[8]; b9 = operand[9];
  //   b10 = operand[10]; b11 = operand[11]; b12 = operand[12]; b13 = operand[13]; b14 = operand[14];
  //   b15 = operand[15]; b16 = operand[16]; b17 = operand[17]; b18 = operand[18]; b19 = operand[19];
  //   b20 = operand[20]; b21 = operand[21]; b22 = operand[22]; b23 = operand[23]; b24 = operand[24];
  //   b25 = operand[25]; b26 = operand[26]; b27 = operand[27]; b28 = operand[28]; b29 = operand[29];
  //   b30 = operand[30]; b31 = operand[31]

  // Notes on the sheet:
  //   This circuit flips the sign of the input when "flip" is true, else it remains unchanged
  //   Split 32 bit number into component bits ->
  //   If flip sign is true, flip all the bits
  //   <- Combine all bits into 32 bit bus
  //   Add 1 to flipped bits if flip is true
  //   Output sign flipped value
endmodule

module InstructionDecoder (
  input  [31:0] instructionIn,
  output [4:0] A_Location,
  output [4:0] B_Location,
  output ImmediateSelect,
  output [31:0] Immediate,
  output Unsigned,
  output SubtractEnable,
  output [4:0] writeSelect,
  output writeEnable,
  output [2:0] resultSelect,
  output error,
  output branchInst,
  output [2:0] branchType,
  output jumpLink,
  output jumpRegister,
  output load,
  output loadUnsigned,
  output store,
  output [1:0] memLength,
  output auipcInst
);

  wire add_flag, addi_flag, beq_flag, bge_flag, bgeu_flag, blt_flag, bltu_flag, bne_flag, BTYPE,
       comparator_1_eq, comparator_2_eq, comparator_3_eq, comparator_4_eq, comparator_5_eq, comparator_6_eq,
       comparator_7_eq, comparator_8_eq, comparator_9_eq, comparator_10_eq, comparator_11_eq,
       comparator_12_eq, comparator_13_eq, comparator_14_eq, comparator_15_eq, comparator_16_eq,
       comparator_17_eq, comparator_18_eq, comparator_19_eq, comparator_20_eq, comparator_21_eq,
       comparator_22_eq, comparator_23_eq, comparator_24_eq, comparator_25_eq, comparator_26_eq,
       comparator_27_eq, comparator_28_eq, comparator_29_eq, comparator_30_eq, comparator_31_eq,
       comparator_32_eq, comparator_33_eq, comparator_36_eq, comparator_37_eq, comparator_38_eq,
       comparator_39_eq, comparator_40_eq, comparator_41_eq, comparator_42_eq, comparator_43_eq,
       comparator_44_eq, comparator_45_eq, comparator_46_eq, comparator_47_eq, comparator_49_eq,
       comparator_50_eq, comparator_51_eq, comparator_52_eq, div_flag, divu_flag, lb_flag, lbu_flag, lh_flag,
       lhu_flag, lui_flag, lw_flag, mul_flag, nor_1_out, nor_3_out, or_1_out, or_4_out, or_5_out, or_6_out,
       or_7_out, or_9_out, or_10_out, or_11_out, rem_flag, remu_flag, sb_flag, sh_flag, slt_flag, slti_flag,
       sltiu_flag, sltu_flag, sw_flag;
  wire [2:0] priority_encoder_1_out;

  Comparator #(.width(7), .mode("unsigned")) comparator_1 (
    .a(instructionIn[6:0]), .b(7'b0010011), .eq(comparator_1_eq));  // open: gt, lt
  Comparator #(.width(3), .mode("unsigned")) comparator_2 (
    .a(instructionIn[14:12]), .b(3'b000), .eq(comparator_2_eq));  // open: gt, lt
  Comparator #(.width(7), .mode("unsigned")) comparator_3 (
    .a(instructionIn[6:0]), .b(7'b0110011), .eq(comparator_3_eq));  // open: gt, lt
  Comparator #(.width(3), .mode("unsigned")) comparator_4 (
    .a(instructionIn[14:12]), .b(3'b000), .eq(comparator_4_eq));  // open: gt, lt
  Comparator #(.width(7), .mode("unsigned")) comparator_5 (
    .a(instructionIn[31:25]), .b({7{1'b0}}), .eq(comparator_5_eq));  // open: gt, lt
  Comparator #(.width(7), .mode("unsigned")) comparator_6 (
    .a(instructionIn[6:0]), .b(7'b0110011), .eq(comparator_6_eq));  // open: gt, lt
  Comparator #(.width(3), .mode("unsigned")) comparator_7 (
    .a(instructionIn[14:12]), .b(3'b000), .eq(comparator_7_eq));  // open: gt, lt
  Comparator #(.width(7), .mode("unsigned")) comparator_8 (
    .a(instructionIn[31:25]), .b(7'b0100000), .eq(comparator_8_eq));  // open: gt, lt
  Comparator #(.width(7), .mode("unsigned")) comparator_9 (
    .a(instructionIn[6:0]), .b(7'b0110011), .eq(comparator_9_eq));  // open: gt, lt
  Comparator #(.width(3), .mode("unsigned")) comparator_10 (
    .a(instructionIn[14:12]), .b(3'b000), .eq(comparator_10_eq));  // open: gt, lt
  Comparator #(.width(7), .mode("unsigned")) comparator_11 (
    .a(instructionIn[31:25]), .b(7'b0000001), .eq(comparator_11_eq));  // open: gt, lt
  Comparator #(.width(7), .mode("unsigned")) comparator_12 (
    .a(instructionIn[6:0]), .b(7'b0110011), .eq(comparator_12_eq));  // open: gt, lt
  Comparator #(.width(3), .mode("unsigned")) comparator_13 (
    .a(instructionIn[14:12]), .b(3'b100), .eq(comparator_13_eq));  // open: gt, lt
  Comparator #(.width(7), .mode("unsigned")) comparator_14 (
    .a(instructionIn[31:25]), .b(7'b0000001), .eq(comparator_14_eq));  // open: gt, lt
  Comparator #(.width(7), .mode("unsigned")) comparator_15 (
    .a(instructionIn[6:0]), .b(7'b0110011), .eq(comparator_15_eq));  // open: gt, lt
  Comparator #(.width(3), .mode("unsigned")) comparator_16 (
    .a(instructionIn[14:12]), .b(3'b101), .eq(comparator_16_eq));  // open: gt, lt
  Comparator #(.width(7), .mode("unsigned")) comparator_17 (
    .a(instructionIn[31:25]), .b(7'b0000001), .eq(comparator_17_eq));  // open: gt, lt
  Comparator #(.width(7), .mode("unsigned")) comparator_18 (
    .a(instructionIn[6:0]), .b(7'b0110011), .eq(comparator_18_eq));  // open: gt, lt
  Comparator #(.width(3), .mode("unsigned")) comparator_19 (
    .a(instructionIn[14:12]), .b(3'b110), .eq(comparator_19_eq));  // open: gt, lt
  Comparator #(.width(7), .mode("unsigned")) comparator_20 (
    .a(instructionIn[31:25]), .b(7'b0000001), .eq(comparator_20_eq));  // open: gt, lt
  Comparator #(.width(7), .mode("unsigned")) comparator_21 (
    .a(instructionIn[6:0]), .b(7'b0110011), .eq(comparator_21_eq));  // open: gt, lt
  Comparator #(.width(3), .mode("unsigned")) comparator_22 (
    .a(instructionIn[14:12]), .b(3'b111), .eq(comparator_22_eq));  // open: gt, lt
  Comparator #(.width(7), .mode("unsigned")) comparator_23 (
    .a(instructionIn[31:25]), .b(7'b0000001), .eq(comparator_23_eq));  // open: gt, lt
  Comparator #(.width(7), .mode("unsigned")) comparator_24 (
    .a(instructionIn[6:0]), .b(7'b0010011), .eq(comparator_24_eq));  // open: gt, lt
  Comparator #(.width(3), .mode("unsigned")) comparator_25 (
    .a(instructionIn[14:12]), .b(3'b010), .eq(comparator_25_eq));  // open: gt, lt
  Comparator #(.width(7), .mode("unsigned")) comparator_26 (
    .a(instructionIn[6:0]), .b(7'b0010011), .eq(comparator_26_eq));  // open: gt, lt
  Comparator #(.width(3), .mode("unsigned")) comparator_27 (
    .a(instructionIn[14:12]), .b(3'b011), .eq(comparator_27_eq));  // open: gt, lt
  Comparator #(.width(7), .mode("unsigned")) comparator_28 (
    .a(instructionIn[6:0]), .b(7'b0110011), .eq(comparator_28_eq));  // open: gt, lt
  Comparator #(.width(3), .mode("unsigned")) comparator_29 (
    .a(instructionIn[14:12]), .b(3'b010), .eq(comparator_29_eq));  // open: gt, lt
  Comparator #(.width(7), .mode("unsigned")) comparator_30 (
    .a(instructionIn[31:25]), .b({7{1'b0}}), .eq(comparator_30_eq));  // open: gt, lt
  Comparator #(.width(7), .mode("unsigned")) comparator_31 (
    .a(instructionIn[6:0]), .b(7'b0110011), .eq(comparator_31_eq));  // open: gt, lt
  Comparator #(.width(3), .mode("unsigned")) comparator_32 (
    .a(instructionIn[14:12]), .b(3'b011), .eq(comparator_32_eq));  // open: gt, lt
  Comparator #(.width(7), .mode("unsigned")) comparator_33 (
    .a(instructionIn[31:25]), .b({7{1'b0}}), .eq(comparator_33_eq));  // open: gt, lt
  Comparator #(.width(7), .mode("unsigned")) comparator_34 (
    .a(instructionIn[6:0]), .b(7'b1101111), .eq(jumpLink));  // open: gt, lt
  Comparator #(.width(7), .mode("unsigned")) comparator_35 (
    .a(instructionIn[6:0]), .b(7'b1100111), .eq(jumpRegister));  // open: gt, lt
  Comparator #(.width(7), .mode("unsigned")) comparator_36 (
    .a(instructionIn[6:0]), .b(7'b1100011), .eq(comparator_36_eq));  // open: gt, lt
  Comparator #(.width(3), .mode("unsigned")) comparator_37 (
    .a(instructionIn[14:12]), .b(3'b000), .eq(comparator_37_eq));  // open: gt, lt
  Comparator #(.width(7), .mode("unsigned")) comparator_38 (
    .a(instructionIn[6:0]), .b(7'b1100011), .eq(comparator_38_eq));  // open: gt, lt
  Comparator #(.width(3), .mode("unsigned")) comparator_39 (
    .a(instructionIn[14:12]), .b(3'b001), .eq(comparator_39_eq));  // open: gt, lt
  Comparator #(.width(7), .mode("unsigned")) comparator_40 (
    .a(instructionIn[6:0]), .b(7'b1100011), .eq(comparator_40_eq));  // open: gt, lt
  Comparator #(.width(3), .mode("unsigned")) comparator_41 (
    .a(instructionIn[14:12]), .b(3'b100), .eq(comparator_41_eq));  // open: gt, lt
  Comparator #(.width(7), .mode("unsigned")) comparator_42 (
    .a(instructionIn[6:0]), .b(7'b1100011), .eq(comparator_42_eq));  // open: gt, lt
  Comparator #(.width(3), .mode("unsigned")) comparator_43 (
    .a(instructionIn[14:12]), .b(3'b101), .eq(comparator_43_eq));  // open: gt, lt
  Comparator #(.width(7), .mode("unsigned")) comparator_44 (
    .a(instructionIn[6:0]), .b(7'b1100011), .eq(comparator_44_eq));  // open: gt, lt
  Comparator #(.width(3), .mode("unsigned")) comparator_45 (
    .a(instructionIn[14:12]), .b(3'b110), .eq(comparator_45_eq));  // open: gt, lt
  Comparator #(.width(7), .mode("unsigned")) comparator_46 (
    .a(instructionIn[6:0]), .b(7'b1100011), .eq(comparator_46_eq));  // open: gt, lt
  Comparator #(.width(3), .mode("unsigned")) comparator_47 (
    .a(instructionIn[14:12]), .b(3'b111), .eq(comparator_47_eq));  // open: gt, lt
  Comparator #(.width(7), .mode("unsigned")) comparator_48 (
    .a(instructionIn[6:0]), .b(7'b0000011), .eq(load));  // open: gt, lt
  Comparator #(.width(7), .mode("unsigned")) comparator_49 (
    .a(instructionIn[6:0]), .b(7'b0000011), .eq(comparator_49_eq));  // open: gt, lt
  Comparator #(.width(3), .mode("unsigned")) comparator_50 (
    .a(instructionIn[14:12]), .b(3'b100), .eq(comparator_50_eq));  // open: gt, lt
  Comparator #(.width(7), .mode("unsigned")) comparator_51 (
    .a(instructionIn[6:0]), .b(7'b0000011), .eq(comparator_51_eq));  // open: gt, lt
  Comparator #(.width(3), .mode("unsigned")) comparator_52 (
    .a(instructionIn[14:12]), .b(3'b101), .eq(comparator_52_eq));  // open: gt, lt
  Comparator #(.width(3), .mode("unsigned")) comparator_53 (
    .a(instructionIn[14:12]), .b(3'b000), .eq(lb_flag));  // open: gt, lt
  Comparator #(.width(3), .mode("unsigned")) comparator_54 (
    .a(instructionIn[14:12]), .b(3'b001), .eq(lh_flag));  // open: gt, lt
  Comparator #(.width(3), .mode("unsigned")) comparator_55 (
    .a(instructionIn[14:12]), .b(3'b010), .eq(lw_flag));  // open: gt, lt
  Comparator #(.width(7), .mode("unsigned")) comparator_56 (
    .a(instructionIn[6:0]), .b(7'b0100011), .eq(store));  // open: gt, lt
  Comparator #(.width(3), .mode("unsigned")) comparator_57 (
    .a(instructionIn[14:12]), .b(3'b000), .eq(sb_flag));  // open: gt, lt
  Comparator #(.width(3), .mode("unsigned")) comparator_58 (
    .a(instructionIn[14:12]), .b(3'b001), .eq(sh_flag));  // open: gt, lt
  Comparator #(.width(3), .mode("unsigned")) comparator_59 (
    .a(instructionIn[14:12]), .b(3'b010), .eq(sw_flag));  // open: gt, lt
  Comparator #(.width(7), .mode("unsigned")) comparator_60 (
    .a(instructionIn[6:0]), .b(7'b0110111), .eq(lui_flag));  // open: gt, lt
  Comparator #(.width(7), .mode("unsigned")) comparator_61 (
    .a(instructionIn[6:0]), .b(7'b0010111), .eq(auipcInst));  // open: gt, lt
  and and_1 (addi_flag, comparator_1_eq, comparator_2_eq);
  and and_2 (add_flag, comparator_3_eq, comparator_4_eq, comparator_5_eq);
  and and_3 (SubtractEnable, comparator_6_eq, comparator_7_eq, comparator_8_eq);
  and and_4 (mul_flag, comparator_9_eq, comparator_10_eq, comparator_11_eq);
  and and_5 (div_flag, comparator_12_eq, comparator_13_eq, comparator_14_eq);
  and and_6 (divu_flag, comparator_15_eq, comparator_16_eq, comparator_17_eq);
  and and_7 (rem_flag, comparator_18_eq, comparator_19_eq, comparator_20_eq);
  and and_8 (remu_flag, comparator_21_eq, comparator_22_eq, comparator_23_eq);
  and and_9 (slti_flag, comparator_24_eq, comparator_25_eq);
  and and_10 (sltiu_flag, comparator_26_eq, comparator_27_eq);
  and and_11 (slt_flag, comparator_28_eq, comparator_29_eq, comparator_30_eq);
  and and_12 (sltu_flag, comparator_31_eq, comparator_32_eq, comparator_33_eq);
  and and_13 (beq_flag, comparator_36_eq, comparator_37_eq);
  and and_14 (bne_flag, comparator_38_eq, comparator_39_eq);
  and and_15 (blt_flag, comparator_40_eq, comparator_41_eq);
  and and_16 (bge_flag, comparator_42_eq, comparator_43_eq);
  and and_17 (bltu_flag, comparator_44_eq, comparator_45_eq);
  and and_18 (bgeu_flag, comparator_46_eq, comparator_47_eq);
  and and_19 (lbu_flag, comparator_49_eq, comparator_50_eq);
  and and_20 (lhu_flag, comparator_51_eq, comparator_52_eq);
  Multiplexer #(.width(5), .enable("false")) multiplexer_1 (
    .in0(instructionIn[19:15]), .in1({5{1'b0}}), .out(A_Location), .sel(lui_flag));
  or or_1 (or_1_out, lui_flag, auipcInst);
  or or_2 (ImmediateSelect, addi_flag, slti_flag, sltiu_flag, jumpLink, BTYPE, load, store, jumpRegister, lui_flag, auipcInst);
  Comparator #(.width(7), .mode("unsigned")) comparator_62 (
    .a(instructionIn[6:0]), .b(7'b1100011), .eq(BTYPE));  // open: gt, lt
  Multiplexer #(.select(3), .width(32), .enable("false")) multiplexer_2 (
    .in0({{21{instructionIn[31]}}, instructionIn[30:20]}),
    .in1({{12{instructionIn[31]}}, instructionIn[19:12], instructionIn[20], instructionIn[30:21], 1'b0}),
    .in2({{20{instructionIn[31]}}, instructionIn[7], instructionIn[30:25], instructionIn[11:8], 1'b0}),
    .in3({{21{instructionIn[31]}}, instructionIn[30:25], instructionIn[11:7]}),
    .in4({instructionIn[31:12], {12{1'b0}}}), .out(Immediate), .sel(priority_encoder_1_out));  // open: in5, in6, in7
  nor nor_1 (nor_1_out, auipcInst, lui_flag, jumpLink, BTYPE, store);
  or or_3 (Unsigned, divu_flag, remu_flag, sltiu_flag, sltu_flag, bltu_flag, bgeu_flag);
  nor nor_2 (writeEnable, BTYPE, store);
  or or_4 (or_4_out, load, store, BTYPE, jumpLink, jumpRegister, addi_flag, add_flag, SubtractEnable, lui_flag, auipcInst);
  or or_5 (or_5_out, div_flag, divu_flag);
  or or_6 (or_6_out, rem_flag, remu_flag);
  or or_7 (or_7_out, slti_flag, sltiu_flag, slt_flag, sltu_flag);
  Comparator #(.width(7), .mode("unsigned")) comparator_63 (
    .a(instructionIn[6:0]), .b(7'b1100011), .eq(branchInst));  // open: gt, lt
  nor nor_3 (nor_3_out, beq_flag, bne_flag, blt_flag, bge_flag, bltu_flag, bgeu_flag);
  or or_8 (loadUnsigned, lbu_flag, lhu_flag);
  or or_9 (or_9_out, lbu_flag, lb_flag, sb_flag);
  or or_10 (or_10_out, lhu_flag, lh_flag, sh_flag);
  or or_11 (or_11_out, lw_flag, sw_flag);
  Priority_Encoder priority_encoder_1 (
    .in0(nor_1_out), .in1(jumpLink), .in2(BTYPE), .in3(store), .in4(or_1_out), .in5(1'b0), .in6(1'b0),
    .in7(1'b0), .out(priority_encoder_1_out), .en_in(1'b1));  // open: gs, en_out
  Priority_Encoder #(.disabled(0)) priority_encoder_2 (
    .in0(or_4_out), .in1(mul_flag), .in2(or_5_out), .in3(or_6_out), .in4(1'b0), .in5(1'b0), .in6(or_7_out),
    .in7(1'b0), .out(resultSelect), .en_in(1'b1), .en_out(error));  // open: gs
  Priority_Encoder #(.disabled(0)) priority_encoder_3 (
    .in0(nor_3_out), .in1(beq_flag), .in2(bne_flag), .in3(blt_flag), .in4(bge_flag), .in5(bltu_flag),
    .in6(bgeu_flag), .in7(1'b0), .out(branchType), .en_in(1'b1));  // open: gs, en_out
  Priority_Encoder #(.select(2), .disabled(0)) priority_encoder_4 (
    .in0(or_9_out), .in1(or_10_out), .in2(1'b0), .in3(or_11_out), .out(memLength), .en_in(1'b1));  // open: gs, en_out
  // Probe on Immediate

  assign B_Location = instructionIn[24:20];
  assign writeSelect = instructionIn[11:7];

  // Other names for the same wires on the sheet: auipc_flag = auipcInst; branch_flag = branchInst;
  //   im_11 = instructionIn[7]; imm_4_0[4:0] = instructionIn[11:7];
  //   immext_btype[31:1] = {{20{instructionIn[31]}}, instructionIn[7], instructionIn[30:25], instructionIn[11:8]};
  //   immext_stype[31:0] = {{21{instructionIn[31]}}, instructionIn[30:25], instructionIn[11:7]};
  //   rd[4:0] = instructionIn[11:7]; imm_4_1[3:0] = instructionIn[11:8]; funct3[2:0] = instructionIn[14:12];
  //   imm_19_12[7:0] = instructionIn[19:12]; imm_31_12[19:0] = instructionIn[31:12];
  //   immext_jtype[31:1] = {{12{instructionIn[31]}}, instructionIn[19:12], instructionIn[20], instructionIn[30:21]};
  //   immext_utype[31:12] = instructionIn[31:12]; rs1[4:0] = instructionIn[19:15]; imm_11 = instructionIn[20];
  //   imm_11_0[11:0] = instructionIn[31:20]; immext_itype[31:0] = {{21{instructionIn[31]}}, instructionIn[30:20]};
  //   rs2[4:0] = instructionIn[24:20]; imm_10_1[9:0] = instructionIn[30:21]; funct7[6:0] = instructionIn[31:25];
  //   imm_10_5[5:0] = instructionIn[30:25]; imm_11_5[6:0] = instructionIn[31:25]; im_12 = instructionIn[31];
  //   imm_20 = instructionIn[31]; opcode[6:0] = instructionIn[6:0]; jal_flag = jumpLink; jalr_flag = jumpRegister;
  //   load_flag = load; store_flag = store; sub_flag = SubtractEnable; UnsupportedInstruction = error

  // Notes on the sheet:
  //   Opcodes
  //   funct3
  //   Hardcoded values of supported opcodes and functions
  //   Split instruction into component parts for all 6 possible format types (spec sec2.3)
  //   R type parsing
  //   I type parsing
  //   B type parsing
  //   U type parsing
  //   funct7
  //   We don't need to check opcodes here since we only care about the width value ->
  //   S type parsing
  //   J type parsing
  //   Check for and parse supported instructions
  //   GreaterThan currently unused
  //   Sign extend immediate input
  //   Equals currently unused
  //   Extra unused option
  //   Produce output control signals based on instruction
  //   Encode branch type
  //   Encode resultSelect signal
  //   OutputPins
endmodule

// Instruction Frame
module InstructionFrame (
  input  [31:0] aOperand_in,
  input  [4:0] aLoc_in,
  input  [31:0] bOperand_in,
  input  [4:0] bLoc_in,
  input  [31:0] immediateVal_in,
  input  immediateSelect_in,
  input  unsignedSelect_in,
  input  subtractEnable_in,
  input  [2:0] resultSelect_in,
  input  [4:0] writeSelect_in,
  input  writeEnable_in,
  input  branchInst_in,
  input  [2:0] branchType_in,
  input  jumpLink_in,
  input  jumpRegister_in,
  input  [31:0] aOpCompare_in,
  input  [31:0] bOpCompare_in,
  input  load_In,
  input  loadUnsigned_In,
  input  store_In,
  input  [1:0] memLength_In,
  input  [31:0] storeData_in,
  input  auipc_In,
  input  writebackState,
  input  memReadState,
  input  executeState,
  input  setupState,
  input  decodeState,
  input  fetch_ReceiveState,
  input  fetch_RequestState,
  input  clk,
  input  reset,
  output [31:0] aOperand_out,
  output [4:0] aLoc_out,
  output [31:0] bOperand_out,
  output [4:0] bLoc_out,
  output [31:0] immediateVal_out,
  output immediateSelect_out,
  output unsignedSelect_out,
  output subtractEnable_out,
  output [2:0] ResultSelect_Out,
  output [4:0] WriteSelect_Out,
  output WriteEnable_Out,
  output branchInst_out,
  output [2:0] branchType_Out,
  output jumpLInk_Out,
  output jumpRegister_Out,
  output [31:0] AOpCompare_Out,
  output [31:0] BOpCompare_Out,
  output load_Out,
  output loadUnsigned_Out,
  output store_Out,
  output [1:0] memLength_Out,
  output [31:0] storeData_Out,
  output auipc_Out
);

  Register #(.width(32)) A_Operand (.D(aOperand_in), .en(setupState), .Q(aOperand_out), .clk(clk), .clr(reset));
  Register #(.width(32)) B_Operand (.D(bOperand_in), .en(setupState), .Q(bOperand_out), .clk(clk), .clr(reset));
  Register #(.width(32)) Immediate (
    .D(immediateVal_in), .en(decodeState), .Q(immediateVal_out), .clk(clk), .clr(reset));
  Register #(.width(1)) Unsigned (
    .D(unsignedSelect_in), .en(decodeState), .Q(unsignedSelect_out), .clk(clk), .clr(reset));
  Register #(.width(3)) ResultSelect (
    .D(resultSelect_in), .en(decodeState), .Q(ResultSelect_Out), .clk(clk), .clr(reset));
  Register #(.width(5)) WriteSelect (.D(writeSelect_in), .en(decodeState), .Q(WriteSelect_Out), .clk(clk), .clr(reset));
  Register #(.width(1)) jumpLink (.D(jumpLink_in), .en(decodeState), .Q(jumpLInk_Out), .clk(clk), .clr(reset));
  Register #(.width(32)) A_OpCompare (.D(aOpCompare_in), .en(setupState), .Q(AOpCompare_Out), .clk(clk), .clr(reset));
  Register #(.width(32)) B_OpCompare (.D(bOpCompare_in), .en(setupState), .Q(BOpCompare_Out), .clk(clk), .clr(reset));
  Register #(.width(1)) Load (.D(load_In), .en(decodeState), .Q(load_Out), .clk(clk), .clr(reset));
  Register #(.width(1)) Store (.D(store_In), .en(decodeState), .Q(store_Out), .clk(clk), .clr(reset));
  Register #(.width(1)) Auipc (.D(auipc_In), .en(decodeState), .Q(auipc_Out), .clk(clk), .clr(reset));
  Register #(.width(5)) A_Location (.D(aLoc_in), .en(decodeState), .Q(aLoc_out), .clk(clk), .clr(reset));
  Register #(.width(5)) B_Location (.D(bLoc_in), .en(decodeState), .Q(bLoc_out), .clk(clk), .clr(reset));
  Register #(.width(1)) ImmediateSelect (
    .D(immediateSelect_in), .en(decodeState), .Q(immediateSelect_out), .clk(clk), .clr(reset));
  Register #(.width(1)) SubtractEnable (
    .D(subtractEnable_in), .en(decodeState), .Q(subtractEnable_out), .clk(clk), .clr(reset));
  Register #(.width(1)) branchInst (.D(branchInst_in), .en(decodeState), .Q(branchInst_out), .clk(clk), .clr(reset));
  Register #(.width(1)) WriteEnable (.D(writeEnable_in), .en(decodeState), .Q(WriteEnable_Out), .clk(clk), .clr(reset));
  Register #(.width(1)) jumpRegister (
    .D(jumpRegister_in), .en(decodeState), .Q(jumpRegister_Out), .clk(clk), .clr(reset));
  Register #(.width(3)) branchType (.D(branchType_in), .en(decodeState), .Q(branchType_Out), .clk(clk), .clr(reset));
  Register #(.width(2)) MemLength (.D(memLength_In), .en(decodeState), .Q(memLength_Out), .clk(clk), .clr(reset));
  Register #(.width(1)) LoadUnsigned (
    .D(loadUnsigned_In), .en(decodeState), .Q(loadUnsigned_Out), .clk(clk), .clr(reset));
  Register #(.width(32)) StoreData (.D(storeData_in), .en(setupState), .Q(storeData_Out), .clk(clk), .clr(reset));

  // Other names for the same wires on the sheet: rst = reset; WreteSelect_Out[4:0] = WriteSelect_Out

  // Notes on the sheet:
  //   Input Pin Connections
  //   Data In
  //   Write Emable In
  //   Clock and Reset
  //   Frame Data Registers
  //   Output Pin Connections
  //   Data Out
endmodule

module PipelineStateController (
  input  loadInst,
  input  clk,
  input  reset,
  output fetch_RequestState,
  output fetch_ReceiveState,
  output decodeState,
  output setupState,
  output executeState,
  output memReadState,
  output writebackState
);

  wire and_1_out, or_1_out;
  wire [2:0] adder_1_out, nextPipelineState, pipelineState;

  Register #(.width(3)) PipeplineState (.D(nextPipelineState), .en(1'b1), .Q(pipelineState), .clk(clk), .clr(reset));
  Adder_part #(.width(3)) adder_1 (.a(pipelineState), .b(3'b001), .out(adder_1_out), .cin(1'b0));  // open: cout
  and and_1 (and_1_out, executeState, ~loadInst);  // AND_Gate
  Multiplexer #(.width(3), .enable("false")) multiplexer_1 (
    .in0(adder_1_out), .in1(3'b000), .out(nextPipelineState), .sel(or_1_out));
  or or_1 (or_1_out, and_1_out, memReadState);
  Decoder #(.select(3), .enable("false")) decoder_1 (
    .out0(writebackState), .out1(fetch_RequestState), .out2(fetch_ReceiveState), .out3(decodeState),
    .out4(setupState), .out5(executeState), .out6(memReadState), .sel(pipelineState));  // open: out7

  // Other names for the same wires on the sheet: Writeback_State = writebackState

  // Notes on the sheet:
  //   Input Pin Connections
  //   Increment pipeline state
  //   Reset state when state=6
  //   Decode pipeline states
  //   Output Pin Connections
endmodule

module instructionFetchController (
  input  [31:0] memoryIn,
  input  cir_writeEnable,
  input  [31:0] pcOverwrite,
  input  pc_writeEnable,
  input  [2:0] branchType,
  input  jumpInst,
  input  compareGreater,
  input  compareEquals,
  input  compareLess,
  input  clk,
  input  reset,
  output [31:0] instructionOut,
  output [31:0] programCounter,
  output [31:0] programCounter_next
);

  wire and_1_out, and_2_out, and_3_out, and_4_out, and_5_out, and_6_out, beqFlag, bgeFlag, bgeuFlag, bltFlag,
       bltuFlag, bneFlag, pcOverwrite_en;
  wire [31:0] multiplexer_1_out;

  Multiplexer #(.width(32), .enable("false")) multiplexer_1 (
    .in0(programCounter_next), .in1(pcOverwrite), .out(multiplexer_1_out), .sel(pcOverwrite_en));
  Register #(.width(32)) PC (.D(multiplexer_1_out), .en(pc_writeEnable), .Q(programCounter), .clk(clk), .clr(reset));
  Register #(.width(32)) CIR (.D(memoryIn), .en(cir_writeEnable), .Q(instructionOut), .clk(clk), .clr(reset));
  Decoder #(.select(3), .enable("false")) decoder_1 (
    .out1(beqFlag), .out2(bneFlag), .out3(bltFlag), .out4(bgeFlag), .out5(bltuFlag), .out6(bgeuFlag),
    .sel(branchType));  // open: out0, out7
  Adder_part #(.width(32)) adder_1 (
    .a(programCounter), .b(32'h4), .out(programCounter_next), .cin(1'b0));  // open: cout
  and and_1 (and_1_out, beqFlag, compareEquals);
  and and_2 (and_2_out, bneFlag, ~compareEquals);  // AND_Gate
  and and_3 (and_3_out, bltFlag, compareLess);
  and and_4 (and_4_out, bgeFlag, compareGreater);
  and and_5 (and_5_out, bltuFlag, compareLess);
  and and_6 (and_6_out, bgeuFlag, compareGreater);
  or or_1 (pcOverwrite_en, jumpInst, and_1_out, and_2_out, and_3_out, and_4_out, and_5_out, and_6_out);

  // Notes on the sheet:
  //   Input Pin Connections
  //   Current Instruction Register (CIR)
  //   Increment Program Counter (PC) after each instruction, unless it is overwritten
  //   Determine if we should overwrite PC for control flow instructions
  //   Output Pin Connections
endmodule

module MainMemory (
  input  [31:0] addressIn,
  input  [31:0] dataIn,
  input  [3:0] byteSelect,
  input  store,
  input  load,
  input  clk,
  input  reset,
  output [31:0] dataOut
);

  wire [31:0] memIn;

  // Probe on addressIn
  // Probe on dataIn
  RAM #(.addrWidth(24), .dataWidth(32), .bus("separate")) ram_1 (
    .addr(addressIn[25:2]), .din(memIn), .data(dataOut), .str(store), .sel(1'b1), .clk(clk), .ld(1'b1));  // open: clr
  Multiplexer #(.width(8), .enable("false")) multiplexer_1 (
    .in0(dataOut[7:0]), .in1(dataIn[7:0]), .out(memIn[7:0]), .sel(byteSelect[0]));
  Multiplexer #(.width(8), .enable("false")) multiplexer_2 (
    .in0(dataOut[15:8]), .in1(dataIn[15:8]), .out(memIn[15:8]), .sel(byteSelect[1]));
  Multiplexer #(.width(8), .enable("false")) multiplexer_3 (
    .in0(dataOut[23:16]), .in1(dataIn[23:16]), .out(memIn[23:16]), .sel(byteSelect[2]));
  Multiplexer #(.width(8), .enable("false")) multiplexer_4 (
    .in0(dataOut[31:24]), .in1(dataIn[31:24]), .out(memIn[31:24]), .sel(byteSelect[3]));
  // Probe on dataOut

  // Other names for the same wires on the sheet: addresIn[31:0] = addressIn; addresLower[1:0] = addressIn[1:0];
  //   B0_write = byteSelect[0]; B1_write = byteSelect[1]; B2_write = byteSelect[2]; B3_write = byteSelect[3];
  //   input_byte0[7:0] = dataIn[7:0]; input_byte1[7:0] = dataIn[15:8]; input_byte2[7:0] = dataIn[23:16];
  //   input_byte3[7:0] = dataIn[31:24]; memCurrent_byte0[7:0] = dataOut[7:0]; memCurrent_byte1[7:0] = dataOut[15:8];
  //   memCurrent_byte2[7:0] = dataOut[23:16]; memCurrent_byte3[7:0] = dataOut[31:24]; memIn_byte0[7:0] = memIn[7:0];
  //   memIn_byte1[7:0] = memIn[15:8]; memIn_byte2[7:0] = memIn[23:16]; memIn_byte3[7:0] = memIn[31:24]

  // Notes on the sheet:
  //   Inputs
  //   RAM (note: this does not behave like real memory)
  //   Determine which bytes to keep and which to overwrite
  //   Outputs
endmodule

module memoryController (
  input  [31:0] addressIn,
  input  [31:0] dataWriteIn,
  input  [1:0] length,
  input  storeIn,
  input  loadIn,
  input  loadUnsigned,
  input  [31:0] ramDataRead,
  input  clk,
  input  reset,
  output [31:0] addressOut,
  output [31:0] ramDataWrite,
  output [3:0] byteSelect,
  output storeOut,
  output loadOut,
  output [31:0] dataReadOut
);

  wire and_1_out, and_2_out, and_3_out, and_4_out, and_11_out, and_12_out, and_13_out, and_16_out,
       and_17_out, and_21_out, and_22_out, and_23_out, comparator_2_eq, comparator_3_eq, comparator_4_gt,
       comparator_5_eq, comparator_6_eq, comparator_7_eq, comparator_8_eq, comparator_9_eq, comparator_10_eq,
       comparator_11_eq, comparator_12_eq, comparator_14_eq, comparator_15_eq, comparator_16_eq,
       comparator_17_eq, comparator_18_eq, comparator_20_eq, comparator_21_gt, comparator_23_eq,
       comparator_24_eq, comparator_25_eq, comparator_26_lt, comparator_27_eq, comparator_28_eq,
       comparator_29_eq, comparator_30_eq, comparator_31_eq, comparator_32_eq, comparator_33_eq,
       comparator_34_eq, comparator_35_eq, comparator_36_eq, comparator_37_eq, comparator_38_eq,
       comparator_39_eq, comparator_40_eq, loadUnsigned_latch, nand_1_out, nor_1_out, nor_2_out, nor_3_out,
       not_1_out, or_1_out, ri1_B0select, ri1_B1select, ri2_B0select, ri2_B2select, ri3_B0select,
       ri3_B1select, ri3_B3select;
  wire [1:0] length_latch, priority_encoder_1_out, priority_encoder_2_out, priority_encoder_3_out,
       priority_encoder_4_out;
  wire [7:7] and_9_out, and_10_out, and_14_out, and_15_out, and_18_out, and_19_out, and_20_out;
  wire [31:0] dataWriteIn_latch;

  // Probe on ramDataRead
  // Probe on dataWriteIn
  or or_1 (or_1_out, storeIn, loadIn, reset);
  _32b_latch u_32b_latch_1 (.D(addressIn), .CLK(or_1_out), .Q(addressOut));
  _32b_latch u_32b_latch_2 (.D(dataWriteIn), .CLK(or_1_out), .Q(dataWriteIn_latch));
  _2b_latch u_2b_latch_1 (.D(length), .CLK(or_1_out), .Q(length_latch));
  D_Latch d_latch_1 (.D(loadUnsigned), .CLK(or_1_out), .Q(loadUnsigned_latch));
  Comparator #(.width(2), .mode("unsigned")) comparator_1 (
    .a(addressOut[1:0]), .b(2'b00), .eq(byteSelect[0]));  // open: gt, lt
  Comparator #(.width(2), .mode("unsigned")) comparator_2 (
    .a(addressOut[1:0]), .b(2'b01), .eq(comparator_2_eq));  // open: gt, lt
  Comparator #(.width(2), .mode("unsigned")) comparator_3 (
    .a(addressOut[1:0]), .b(2'b00), .eq(comparator_3_eq));  // open: gt, lt
  Comparator #(.width(2), .mode("unsigned")) comparator_4 (
    .a(length_latch), .b(2'b00), .gt(comparator_4_gt));  // open: eq, lt
  Comparator #(.width(2), .mode("unsigned")) comparator_5 (
    .a(addressOut[1:0]), .b(2'b10), .eq(comparator_5_eq));  // open: gt, lt
  Comparator #(.width(2), .mode("unsigned")) comparator_6 (
    .a(addressOut[1:0]), .b(2'b00), .eq(comparator_6_eq));  // open: gt, lt
  Comparator #(.width(2), .mode("unsigned")) comparator_7 (
    .a(length_latch), .b(2'b11), .eq(comparator_7_eq));  // open: gt, lt
  Comparator #(.width(2), .mode("unsigned")) comparator_8 (
    .a(addressOut[1:0]), .b(2'b11), .eq(comparator_8_eq));  // open: gt, lt
  Comparator #(.width(2), .mode("unsigned")) comparator_9 (
    .a(addressOut[1:0]), .b(2'b10), .eq(comparator_9_eq));  // open: gt, lt
  Comparator #(.width(2), .mode("unsigned")) comparator_10 (
    .a(length_latch), .b(2'b01), .eq(comparator_10_eq));  // open: gt, lt
  Comparator #(.width(2), .mode("unsigned")) comparator_11 (
    .a(addressOut[1:0]), .b(2'b00), .eq(comparator_11_eq));  // open: gt, lt
  Comparator #(.width(2), .mode("unsigned")) comparator_12 (
    .a(length_latch), .b(2'b11), .eq(comparator_12_eq));  // open: gt, lt
  and and_1 (and_1_out, comparator_3_eq, comparator_4_gt);
  and and_2 (and_2_out, comparator_6_eq, comparator_7_eq);
  and and_3 (and_3_out, comparator_9_eq, comparator_10_eq);
  and and_4 (and_4_out, comparator_11_eq, comparator_12_eq);
  or or_2 (byteSelect[1], comparator_2_eq, and_1_out);
  or or_3 (byteSelect[2], comparator_5_eq, and_2_out);
  or or_4 (byteSelect[3], comparator_8_eq, and_3_out, and_4_out);
  Comparator #(.width(2), .mode("unsigned")) comparator_13 (
    .a(addressOut[1:0]), .b(2'b11), .eq(ri3_B0select));  // open: gt, lt
  Comparator #(.width(2), .mode("unsigned")) comparator_14 (
    .a(addressOut[1:0]), .b(2'b10), .eq(comparator_14_eq));  // open: gt, lt
  Comparator #(.width(2), .mode("unsigned")) comparator_15 (
    .a(length_latch), .b(2'b01), .eq(comparator_15_eq));  // open: gt, lt
  Comparator #(.width(2), .mode("unsigned")) comparator_16 (
    .a(addressOut[1:0]), .b(2'b00), .eq(comparator_16_eq));  // open: gt, lt
  Comparator #(.width(2), .mode("unsigned")) comparator_17 (
    .a(length_latch), .b(2'b11), .eq(comparator_17_eq));  // open: gt, lt
  and and_5 (ri3_B1select, comparator_14_eq, comparator_15_eq);
  and and_6 (ri3_B3select, comparator_16_eq, comparator_17_eq);
  Multiplexer #(.width(8), .enable("false")) multiplexer_1 (
    .in0({8{1'b0}}), .in1(dataWriteIn_latch[7:0]), .out(ramDataWrite[7:0]), .sel(comparator_18_eq));
  Comparator #(.width(2), .mode("unsigned")) comparator_18 (
    .a(addressOut[1:0]), .b(2'b00), .eq(comparator_18_eq));  // open: gt, lt
  Multiplexer #(.select(2), .width(8), .enable("false")) multiplexer_2 (
    .in0({8{1'b0}}), .in1(dataWriteIn_latch[7:0]), .in2(dataWriteIn_latch[15:8]), .out(ramDataWrite[15:8]),
    .sel({ri1_B1select, ri1_B0select}));  // open: in3
  Comparator #(.width(2), .mode("unsigned")) comparator_19 (
    .a(addressOut[1:0]), .b(2'b01), .eq(ri1_B0select));  // open: gt, lt
  Comparator #(.width(2), .mode("unsigned")) comparator_20 (
    .a(addressOut[1:0]), .b(2'b00), .eq(comparator_20_eq));  // open: gt, lt
  Comparator #(.width(2), .mode("unsigned")) comparator_21 (
    .a(length_latch), .b(2'b00), .gt(comparator_21_gt));  // open: eq, lt
  Multiplexer #(.select(2), .width(8), .enable("false")) multiplexer_3 (
    .in0({8{1'b0}}), .in1(dataWriteIn_latch[7:0]), .in2(dataWriteIn_latch[23:16]), .out(ramDataWrite[23:16]),
    .sel({ri2_B2select, ri2_B0select}));  // open: in3
  Comparator #(.width(2), .mode("unsigned")) comparator_22 (
    .a(addressOut[1:0]), .b(2'b10), .eq(ri2_B0select));  // open: gt, lt
  Comparator #(.width(2), .mode("unsigned")) comparator_23 (
    .a(addressOut[1:0]), .b(2'b00), .eq(comparator_23_eq));  // open: gt, lt
  Comparator #(.width(2), .mode("unsigned")) comparator_24 (
    .a(length_latch), .b(2'b11), .eq(comparator_24_eq));  // open: gt, lt
  Multiplexer #(.select(2), .width(8), .enable("false")) multiplexer_4 (
    .in0({8{1'b0}}), .in1(dataWriteIn_latch[7:0]), .in2(dataWriteIn_latch[15:8]),
    .in3(dataWriteIn_latch[31:24]), .out(ramDataWrite[31:24]), .sel(priority_encoder_1_out));
  and and_7 (ri1_B1select, comparator_20_eq, comparator_21_gt);
  and and_8 (ri2_B2select, comparator_23_eq, comparator_24_eq);
  nand nand_1 (nand_1_out, ri3_B0select, ri3_B1select, ri3_B3select);
  Priority_Encoder #(.select(2)) priority_encoder_1 (
    .in0(nand_1_out), .in1(ri3_B0select), .in2(ri3_B1select), .in3(ri3_B3select),
    .out(priority_encoder_1_out), .en_in(1'b1));  // open: gs, en_out
  Comparator #(.width(2), .mode("unsigned")) comparator_25 (
    .a(addressOut[1:0]), .b(2'b00), .eq(comparator_25_eq));  // open: gt, lt
  Comparator #(.width(2), .mode("unsigned")) comparator_26 (
    .a(length_latch), .b(2'b01), .lt(comparator_26_lt));  // open: gt, eq
  not not_1 (not_1_out, comparator_26_lt);
  Comparator #(.width(2), .mode("unsigned")) comparator_27 (
    .a(addressOut[1:0]), .b(2'b10), .eq(comparator_27_eq));  // open: gt, lt
  Comparator #(.width(2), .mode("unsigned")) comparator_28 (
    .a(length_latch), .b(2'b01), .eq(comparator_28_eq));  // open: gt, lt
  Comparator #(.width(2), .mode("unsigned")) comparator_29 (
    .a(addressOut[1:0]), .b(2'b10), .eq(comparator_29_eq));  // open: gt, lt
  Comparator #(.width(2), .mode("unsigned")) comparator_30 (
    .a(length_latch), .b(2'b00), .eq(comparator_30_eq));  // open: gt, lt
  Comparator #(.width(2), .mode("unsigned")) comparator_31 (
    .a(addressOut[1:0]), .b(2'b00), .eq(comparator_31_eq));  // open: gt, lt
  Comparator #(.width(2), .mode("unsigned")) comparator_32 (
    .a(length_latch), .b(2'b11), .eq(comparator_32_eq));  // open: gt, lt
  Comparator #(.width(2), .mode("unsigned")) comparator_33 (
    .a(addressOut[1:0]), .b(2'b00), .eq(comparator_33_eq));  // open: gt, lt
  Comparator #(.width(2), .mode("unsigned")) comparator_34 (
    .a(length_latch), .b(2'b01), .eq(comparator_34_eq));  // open: gt, lt
  Comparator #(.width(2), .mode("unsigned")) comparator_35 (
    .a(addressOut[1:0]), .b(2'b00), .eq(comparator_35_eq));  // open: gt, lt
  Comparator #(.width(2), .mode("unsigned")) comparator_36 (
    .a(length_latch), .b(2'b11), .eq(comparator_36_eq));  // open: gt, lt
  Comparator #(.width(2), .mode("unsigned")) comparator_37 (
    .a(addressOut[1:0]), .b(2'b00), .eq(comparator_37_eq));  // open: gt, lt
  Comparator #(.width(2), .mode("unsigned")) comparator_38 (
    .a(length_latch), .b(2'b01), .eq(comparator_38_eq));  // open: gt, lt
  Comparator #(.width(2), .mode("unsigned")) comparator_39 (
    .a(addressOut[1:0]), .b(2'b10), .eq(comparator_39_eq));  // open: gt, lt
  Comparator #(.width(2), .mode("unsigned")) comparator_40 (
    .a(length_latch), .b(2'b01), .eq(comparator_40_eq));  // open: gt, lt
  and and_9 (and_9_out[7], ~loadUnsigned_latch, ramDataRead[7]);  // AND_Gate
  and and_10 (and_10_out[7], ~loadUnsigned_latch, ramDataRead[23]);  // AND_Gate
  and and_11 (and_11_out, comparator_25_eq, not_1_out);
  and and_12 (and_12_out, comparator_27_eq, comparator_28_eq);
  and and_13 (and_13_out, comparator_29_eq, comparator_30_eq);
  and and_14 (and_14_out[7], ~loadUnsigned_latch, ramDataRead[7]);  // AND_Gate
  and and_15 (and_15_out[7], ~loadUnsigned_latch, ramDataRead[15]);  // AND_Gate
  and and_16 (and_16_out, comparator_31_eq, comparator_32_eq);
  and and_17 (and_17_out, comparator_33_eq, comparator_34_eq);
  and and_18 (and_18_out[7], ~loadUnsigned_latch, ramDataRead[7]);  // AND_Gate
  and and_19 (and_19_out[7], ~loadUnsigned_latch, ramDataRead[15]);  // AND_Gate
  and and_20 (and_20_out[7], ~loadUnsigned_latch, ramDataRead[23]);  // AND_Gate
  and and_21 (and_21_out, comparator_35_eq, comparator_36_eq);
  and and_22 (and_22_out, comparator_37_eq, comparator_38_eq);
  and and_23 (and_23_out, comparator_39_eq, comparator_40_eq);
  nor nor_1 (nor_1_out, and_11_out, and_12_out, and_13_out);
  nor nor_2 (nor_2_out, and_16_out, and_17_out);
  nor nor_3 (nor_3_out, and_21_out, and_22_out, and_23_out);
  Multiplexer #(.select(2), .width(8), .enable("false")) multiplexer_5 (
    .in0(ramDataRead[7:0]), .in1(ramDataRead[15:8]), .in2(ramDataRead[23:16]), .in3(ramDataRead[31:24]),
    .out(dataReadOut[7:0]), .sel(addressOut[1:0]));
  Multiplexer #(.select(2), .width(8), .enable("false")) multiplexer_6 (
    .in0(ramDataRead[15:8]), .in1({8{and_9_out[7]}}), .in2(ramDataRead[31:24]), .in3({8{and_10_out[7]}}),
    .out(dataReadOut[15:8]), .sel(priority_encoder_2_out));
  Priority_Encoder #(.select(2)) priority_encoder_2 (
    .in0(and_11_out), .in1(nor_1_out), .in2(and_12_out), .in3(and_13_out), .out(priority_encoder_2_out),
    .en_in(1'b1));  // open: gs, en_out
  Multiplexer #(.select(2), .width(8), .enable("false")) multiplexer_7 (
    .in0(ramDataRead[23:16]), .in1({8{and_14_out[7]}}), .in2({8{and_15_out[7]}}), .out(dataReadOut[23:16]),
    .sel(priority_encoder_3_out));  // open: in3
  Priority_Encoder #(.select(2)) priority_encoder_3 (
    .in0(and_16_out), .in1(nor_2_out), .in2(and_17_out), .in3(1'b0), .out(priority_encoder_3_out),
    .en_in(1'b1));  // open: gs, en_out
  Multiplexer #(.select(2), .width(8), .enable("false")) multiplexer_8 (
    .in0(ramDataRead[31:24]), .in1({8{and_18_out[7]}}), .in2({8{and_19_out[7]}}), .in3({8{and_20_out[7]}}),
    .out(dataReadOut[31:24]), .sel(priority_encoder_4_out));
  Priority_Encoder #(.select(2)) priority_encoder_4 (
    .in0(and_21_out), .in1(nor_3_out), .in2(and_22_out), .in3(and_23_out), .out(priority_encoder_4_out),
    .en_in(1'b1));  // open: gs, en_out
  // Probe on ramDataWrite
  // Probe on dataReadOut

  assign loadOut = loadIn;
  assign storeOut = storeIn;

  // Other names for the same wires on the sheet: addressIn_latch[31:0] = addressOut;
  //   addressLower[1:0] = addressOut[1:0]; B0_write = byteSelect[0]; B1_write = byteSelect[1];
  //   B2_write = byteSelect[2]; B3_write = byteSelect[3]; readOut_byte0[7:0] = dataReadOut[7:0];
  //   readOut_byte1[7:0] = dataReadOut[15:8]; readOut_byte2[7:0] = dataReadOut[23:16];
  //   readOut_byte3[7:0] = dataReadOut[31:24]; input_byte0[7:0] = dataWriteIn_latch[7:0];
  //   input_byte1[7:0] = dataWriteIn_latch[15:8]; input_byte2[7:0] = dataWriteIn_latch[23:16];
  //   input_byte3[7:0] = dataWriteIn_latch[31:24]; ramDataRead_byte0[7:0] = ramDataRead[7:0];
  //   ramDataRead_byte1[7:0] = ramDataRead[15:8]; ramDataRead_byte2[7:0] = ramDataRead[23:16];
  //   ramDataRead_byte3[7:0] = ramDataRead[31:24]; ramIn_byte0[7:0] = ramDataWrite[7:0];
  //   ramIn_byte1[7:0] = ramDataWrite[15:8]; ramIn_byte2[7:0] = ramDataWrite[23:16];
  //   ramIn_byte3[7:0] = ramDataWrite[31:24]

  // Notes on the sheet:
  //   Inputs
  //   Input Buffers
  //   Determine which bytes to write
  //   Rearrange data based on length and address
  //   Sign extend read data based on length
  //   Outputs
endmodule

module D_Latch (
  input  D,
  input  CLK,
  output Q
);

  wire nand_1_out, nand_2_out, nand_4_out;

  nand nand_1 (nand_1_out, D, CLK);
  nand nand_2 (nand_2_out, nand_1_out, CLK);
  nand nand_3 (Q, nand_1_out, nand_4_out);
  nand nand_4 (nand_4_out, Q, nand_2_out);
endmodule

module _32b_latch (
  input  [31:0] D,
  input  CLK,
  output [31:0] Q
);

  D_Latch d_latch_1 (.D(D[0]), .CLK(CLK), .Q(Q[0]));
  D_Latch d_latch_2 (.D(D[1]), .CLK(CLK), .Q(Q[1]));
  D_Latch d_latch_3 (.D(D[2]), .CLK(CLK), .Q(Q[2]));
  D_Latch d_latch_4 (.D(D[3]), .CLK(CLK), .Q(Q[3]));
  D_Latch d_latch_5 (.D(D[4]), .CLK(CLK), .Q(Q[4]));
  D_Latch d_latch_6 (.D(D[5]), .CLK(CLK), .Q(Q[5]));
  D_Latch d_latch_7 (.D(D[6]), .CLK(CLK), .Q(Q[6]));
  D_Latch d_latch_8 (.D(D[7]), .CLK(CLK), .Q(Q[7]));
  D_Latch d_latch_9 (.D(D[8]), .CLK(CLK), .Q(Q[8]));
  D_Latch d_latch_10 (.D(D[9]), .CLK(CLK), .Q(Q[9]));
  D_Latch d_latch_11 (.D(D[10]), .CLK(CLK), .Q(Q[10]));
  D_Latch d_latch_12 (.D(D[11]), .CLK(CLK), .Q(Q[11]));
  D_Latch d_latch_13 (.D(D[12]), .CLK(CLK), .Q(Q[12]));
  D_Latch d_latch_14 (.D(D[13]), .CLK(CLK), .Q(Q[13]));
  D_Latch d_latch_15 (.D(D[14]), .CLK(CLK), .Q(Q[14]));
  D_Latch d_latch_16 (.D(D[15]), .CLK(CLK), .Q(Q[15]));
  D_Latch d_latch_17 (.D(D[16]), .CLK(CLK), .Q(Q[16]));
  D_Latch d_latch_18 (.D(D[17]), .CLK(CLK), .Q(Q[17]));
  D_Latch d_latch_19 (.D(D[18]), .CLK(CLK), .Q(Q[18]));
  D_Latch d_latch_20 (.D(D[19]), .CLK(CLK), .Q(Q[19]));
  D_Latch d_latch_21 (.D(D[20]), .CLK(CLK), .Q(Q[20]));
  D_Latch d_latch_22 (.D(D[21]), .CLK(CLK), .Q(Q[21]));
  D_Latch d_latch_23 (.D(D[22]), .CLK(CLK), .Q(Q[22]));
  D_Latch d_latch_24 (.D(D[23]), .CLK(CLK), .Q(Q[23]));
  D_Latch d_latch_25 (.D(D[24]), .CLK(CLK), .Q(Q[24]));
  D_Latch d_latch_26 (.D(D[25]), .CLK(CLK), .Q(Q[25]));
  D_Latch d_latch_27 (.D(D[26]), .CLK(CLK), .Q(Q[26]));
  D_Latch d_latch_28 (.D(D[27]), .CLK(CLK), .Q(Q[27]));
  D_Latch d_latch_29 (.D(D[28]), .CLK(CLK), .Q(Q[28]));
  D_Latch d_latch_30 (.D(D[29]), .CLK(CLK), .Q(Q[29]));
  D_Latch d_latch_31 (.D(D[30]), .CLK(CLK), .Q(Q[30]));
  D_Latch d_latch_32 (.D(D[31]), .CLK(CLK), .Q(Q[31]));
endmodule

module _2b_latch (
  input  [1:0] D,
  input  CLK,
  output [1:0] Q
);

  D_Latch d_latch_1 (.D(D[0]), .CLK(CLK), .Q(Q[0]));
  D_Latch d_latch_2 (.D(D[1]), .CLK(CLK), .Q(Q[1]));
endmodule

module SOC (
  input  [31:0] memDataRead,
  input  CLK,
  input  RESET,
  output [31:0] memAddress,
  output [31:0] memDataWrite,
  output [3:0] memByteSelect,
  output memStore,
  output memLoad,
  output [31:0] programCounter
);

  wire Pipeline_load, Pipeline_loadunsigned, Pipeline_store;
  wire [1:0] Pipeline_memorylength;
  wire [31:0] MemController_datareadout, Pipeline_memoryaddress, Pipeline_memorydatawrite;

  Pipeline Pipeline (
    .memoryDataRead(MemController_datareadout), .programCounter_out(programCounter),
    .memoryAddress(Pipeline_memoryaddress), .memoryDataWrite(Pipeline_memorydatawrite),
    .memoryLength(Pipeline_memorylength), .store(Pipeline_store), .load(Pipeline_load), .clk(CLK),
    .reset(RESET), .loadUnsigned(Pipeline_loadunsigned));
  memoryController MemController (
    .addressIn(Pipeline_memoryaddress), .dataWriteIn(Pipeline_memorydatawrite),
    .length(Pipeline_memorylength), .storeIn(Pipeline_store), .loadIn(Pipeline_load),
    .ramDataRead(memDataRead), .addressOut(memAddress), .ramDataWrite(memDataWrite),
    .byteSelect(memByteSelect), .storeOut(memStore), .loadOut(memLoad),
    .dataReadOut(MemController_datareadout), .clk(CLK), .loadUnsigned(Pipeline_loadunsigned), .reset(RESET));

  // Notes on the sheet:
  //   Inputs
  //   Outputs
endmodule
