// Logisim project cpu.circ as structural Verilog: 19 circuits, main circuit main
module main (
);

  wire and_1_out, and_2_out, clock_1_out, comparator_1_eq, comparator_2_eq, Core_load, Core_loadunsigned,
       Core_store, MemController_loadout, MemController_storeout, RAM_addressoutofrange, Reset_out;
  wire [1:0] Core_memlength;
  wire [3:0] MemController_byteselect;
  wire [31:0] Core_memaddress, Core_memdatawrite, MemController_memdatain, MemController_readout, PC,
       RAM_ADDRESS, RAM_OUT;

  Comparator #(.width(32)) comparator_1 (.a(PC), .b(RAM_ADDRESS), .eq(comparator_1_eq));  // open: gt, lt
  Comparator #(.width(32)) comparator_2 (.a(RAM_OUT), .b({32{1'b0}}), .eq(comparator_2_eq));  // open: gt, lt
  and and_1 (and_1_out, comparator_1_eq, comparator_2_eq);
  and and_2 (and_2_out, ~and_1_out, clock_1_out);  // AND_Gate
  Clock clock_1 (.out(clock_1_out));
  // Probe on PC
  Core Core (
    .memoryDataRead(MemController_readout), .PC(PC), .memAddress(Core_memaddress),
    .memDataWrite(Core_memdatawrite), .memLength(Core_memlength), .store(Core_store), .load(Core_load),
    .clk(and_2_out), .reset(Reset_out), .loadUnsigned(Core_loadunsigned));  // open: InstMemoryIn
  Button Reset (.out(Reset_out));
  memoryController MemController (
    .addressIn(Core_memaddress), .dataWriteIn(Core_memdatawrite), .length(Core_memlength),
    .storeIn(Core_store), .loadIn(Core_load), .memoryOut(RAM_OUT), .memAddress(RAM_ADDRESS),
    .memDataIn(MemController_memdatain), .byteSelect(MemController_byteselect),
    .storeOut(MemController_storeout), .loadOut(MemController_loadout), .readOut(MemController_readout),
    .clk(and_2_out), .loadUnsigned(Core_loadunsigned), .reset(Reset_out));
  MainMemory RAM (
    .addressIn(RAM_ADDRESS), .dataOut(RAM_OUT), .dataIn(MemController_memdatain),
    .store(MemController_storeout), .load(MemController_loadout), .addressOutOfRange(RAM_addressoutofrange),
    .clk(and_2_out), .byteSelect(MemController_byteselect));  // open: reset
  LED led_1 (.in(RAM_addressoutofrange));
endmodule

module Adder (
  input  [31:0] IN_A,
  input  [31:0] IN_B,
  input  Subtract,
  output [31:0] Result
);

  wire [31:0] adder_1_out, subtractor_1_out;

  Adder_part #(.width(32)) adder_1 (.a(IN_A), .b(IN_B), .out(adder_1_out), .cin(1'b0));  // open: cout
  Subtractor #(.width(32)) subtractor_1 (.a(IN_A), .b(IN_B), .out(subtractor_1_out), .bin(1'b0));  // open: bout
  Multiplexer #(.width(32), .enable("false")) multiplexer_1 (
    .in0(adder_1_out), .in1(subtractor_1_out), .out(Result), .sel(Subtract));

  // Notes on the sheet:
  //   This circuit performs A+B
  //   This circuit performs A-B
  //   MUX used to switch which result we output, + or -
endmodule

module Divider (
  input  [31:0] IN_A,
  input  [31:0] IN_B,
  input  Unsigned,
  output [31:0] Result,
  output [31:0] Remainder
);

  wire A_negative, B_negative, xor_1_out;
  wire [31:0] AbsVal_2_absoluteval, AbsVal_absoluteval, divider_1_out, divider_1_rem;

  AbsoluteValue AbsVal (.IN(IN_A), .Unsigned(Unsigned), .AbsoluteVal(AbsVal_absoluteval), .NegativeInput(A_negative));
  AbsoluteValue AbsVal_2 (
    .IN(IN_B), .Unsigned(Unsigned), .AbsoluteVal(AbsVal_2_absoluteval), .NegativeInput(B_negative));
  Divider_part #(.width(32)) divider_1 (
    .a(AbsVal_absoluteval), .b(AbsVal_2_absoluteval), .out(divider_1_out), .rem(divider_1_rem));  // open: upper
  xor xor_1 (xor_1_out, A_negative, B_negative);
  FlipSign FlipSign (.Flip(xor_1_out), .IN(divider_1_out), .Output(Result));
  FlipSign FlipSign_2 (.Flip(A_negative), .IN(divider_1_rem), .Output(Remainder));

  // Notes on the sheet:
  //   Performs A/B
  //   Take absolute value of inputs
  //   Make result negative if inputs had opposite signs
  //   Make remainder negative if quotient (A) was negative
endmodule

module Core (
  input  [31:0] InstMemoryIn,
  input  [31:0] memoryDataRead,
  input  clk,
  input  reset,
  output [31:0] PC,
  output [31:0] memAddress,
  output [31:0] memDataWrite,
  output [1:0] memLength,
  output store,
  output load,
  output loadUnsigned
);

  wire and_1_out, and_2_out, and_4_out, auipcInst_decode, auipcInst_frame, branchInst_decode,
       branchInst_frame, cir_we, Equals, Execute_State, framewritecontroller_1_aloc_writeenable,
       framewritecontroller_1_aop_writeenable, framewritecontroller_1_auipc_writeenable,
       framewritecontroller_1_bloc_writeenable, framewritecontroller_1_bop_writeenable,
       framewritecontroller_1_branchinst_writeenable, framewritecontroller_1_branchtype_writeenable,
       framewritecontroller_1_imm_writeenable, framewritecontroller_1_immslct_writeenable,
       framewritecontroller_1_jumpinst_writeenable, framewritecontroller_1_load_writeenable,
       framewritecontroller_1_memlength_writeenable, framewritecontroller_1_resultselect_writeenable,
       framewritecontroller_1_store_writeenable, framewritecontroller_1_storedata_writeenable,
       framewritecontroller_1_subenable_writeenable, framewritecontroller_1_unsigned_writeenable,
       framewritecontroller_1_writeenable_writeenable, framewritecontroller_1_writeselect_writeenable,
       GreaterThan, ImmediateSelect_decode, ImmediateSelect_frame, jumpLink_decode, jumpLink_frame,
       jumpRegister_decode, jumpRegister_frame, LessThan, load_decode, load_frame, loadUnsigned_decode,
       or_1_out, or_2_out, pc_we, regWriteEnable, StateController_decode_state, StateController_fetch_state,
       StateController_fetchrequest_state, StateController_memread_state, StateController_setup_state,
       store_decode, store_frame, SubtractEnable_decode, SubtractEnable_frame, Unsigned_decode,
       Unsigned_frame, Writeback_State, WriteEnable_decode, WriteEnable_frame;
  wire [0:0] or_3_out;
  wire [1:0] memLength_decode, memLength_frame;
  wire [2:0] branchType_decode, branchType_frame, resultSelect_decode, resultSelect_frame;
  wire [4:0] A_Location_decode, A_Location_frame, B_Location_decode, B_Location_frame, WriteSelect_decode,
       WriteSelect_frame;
  wire [31:0] A_OpCompare, A_Operand, AdderOut, AOpCompare_frame, AOperand_frame, B_OpCompare, B_Operand,
       BOpCompare_frame, BOperand_frame, DivideOut, Immediate_decode, Immediate_frame, multiplexer_4_out,
       MultiplyOut, pc_instFetch_Controller_instructionout, PC_next, ReadBData, RemainderOut, Result_exec;

  PipelineStateController StateController (
    .loadInst(load_frame), .clk(clk), .reset(reset), .FetchRequest_State(StateController_fetchrequest_state),
    .Fetch_State(StateController_fetch_state), .Decode_State(StateController_decode_state),
    .Setup_State(StateController_setup_state), .Execute_State(Execute_State),
    .memRead_State(StateController_memread_state), .Writeback_State(Writeback_State));
  // Probe on memoryDataRead
  Multiplexer #(.width(32), .enable("false")) multiplexer_1 (
    .in0(ReadBData), .in1(Immediate_frame), .out(B_Operand), .sel(ImmediateSelect_frame));
  and and_1 (and_1_out, ~branchInst_frame, ImmediateSelect_frame);  // AND_Gate
  Multiplexer #(.width(32), .enable("false")) multiplexer_2 (
    .in0(ReadBData), .in1(Immediate_frame), .out(B_OpCompare), .sel(and_1_out));
  or or_1 (or_1_out, jumpLink_frame, jumpRegister_frame);
  // Probe on pc_instFetch_Controller_instructionout
  pc_instFetch_Controller pc_instFetch_Controller (
    .MemoryIn(memoryDataRead), .cir_we(cir_we), .pcOverwrite(Result_exec), .pc_we(pc_we),
    .branchType(branchType_frame), .jumpInst(or_1_out), .compare_greater(GreaterThan),
    .compare_equals(Equals), .compare_less(LessThan), .clk(clk), .reset(reset),
    .InstructionOut(pc_instFetch_Controller_instructionout), .PC(PC), .PC_next(PC_next));
  InstructionDecoder instructiondecoder_1 (
    .InstructionIn(pc_instFetch_Controller_instructionout), .A_Location(A_Location_decode),
    .B_Location(B_Location_decode), .ImmediateSelect(ImmediateSelect_decode), .Immediate(Immediate_decode),
    .Unsigned(Unsigned_decode), .SubtractEnable(SubtractEnable_decode), .writeSelect(WriteSelect_decode),
    .writeEnable(WriteEnable_decode), .resultSelect(resultSelect_decode), .branchInst(branchInst_decode),
    .branchType(branchType_decode), .jumpLink(jumpLink_decode), .jumpRegister(jumpRegister_decode),
    .load(load_decode), .loadUnsigned(loadUnsigned_decode), .store(store_decode),
    .memLength(memLength_decode), .auipcInst(auipcInst_decode));  // open: error
  FrameWriteController framewritecontroller_1 (
    .FetchRequest_State(StateController_fetchrequest_state),
    .FetchReceive_State(StateController_fetch_state), .Decode_State(StateController_decode_state),
    .Setup_State(StateController_setup_state), .Execute_State(Execute_State),
    .memRead_State(StateController_memread_state), .Writeback_State(Writeback_State),
    .AOp_writeEnable(framewritecontroller_1_aop_writeenable),
    .ALoc_writeEnable(framewritecontroller_1_aloc_writeenable),
    .BOp_writeEnable(framewritecontroller_1_bop_writeenable),
    .BLoc_writeEnable(framewritecontroller_1_bloc_writeenable),
    .Imm_writeEnable(framewritecontroller_1_imm_writeenable),
    .ImmSlct_writeEnable(framewritecontroller_1_immslct_writeenable),
    .Unsigned_writeEnable(framewritecontroller_1_unsigned_writeenable),
    .SubEnable_writeEnable(framewritecontroller_1_subenable_writeenable),
    .ResultSelect_writeEnable(framewritecontroller_1_resultselect_writeenable),
    .WriteSelect_writeEnable(framewritecontroller_1_writeselect_writeenable),
    .WriteEnable_writeEnable(framewritecontroller_1_writeenable_writeenable),
    .branchInst_writeEnable(framewritecontroller_1_branchinst_writeenable),
    .branchType_writeEnable(framewritecontroller_1_branchtype_writeenable),
    .jumpInst_writeEnable(framewritecontroller_1_jumpinst_writeenable),
    .load_writeEnable(framewritecontroller_1_load_writeenable),
    .store_writeEnable(framewritecontroller_1_store_writeenable),
    .memLength_writeEnable(framewritecontroller_1_memlength_writeenable),
    .storeData_writeEnable(framewritecontroller_1_storedata_writeenable),
    .auipc_writeEnable(framewritecontroller_1_auipc_writeenable), .Result_writeEnable(regWriteEnable),
    .cir_writeEnable(cir_we), .pc_writeEnable(pc_we));
  InstructionFrame instructionframe_1 (
    .AOp_In(A_Operand), .ALoc_In(A_Location_decode), .BOp_In(B_Operand), .BLoc_In(B_Location_decode),
    .Imm_In(Immediate_decode), .ImmSlct_In(ImmediateSelect_decode), .Unsigned_In(Unsigned_decode),
    .SubEnable_In(SubtractEnable_decode), .ResultSelect_In(resultSelect_decode),
    .WriteSelect_In(WriteSelect_decode), .WriteEnable_In(WriteEnable_decode),
    .branchInst_In(branchInst_decode), .branchType_In(branchType_decode), .jumpLink_In(jumpLink_decode),
    .jumpRegister_In(jumpRegister_decode), .aOpCompare_in(A_OpCompare), .bOpCompare_in(B_OpCompare),
    .load_In(load_decode), .loadUnsigned_In(loadUnsigned_decode), .store_In(store_decode),
    .memLength_In(memLength_decode), .storeData_in(ReadBData), .auipc_In(auipcInst_decode),
    .AOp_writeEnable(framewritecontroller_1_aop_writeenable),
    .ALoc_writeEnable(framewritecontroller_1_aloc_writeenable),
    .BOp_writeEnable(framewritecontroller_1_bop_writeenable),
    .BLoc_writeEnable(framewritecontroller_1_bloc_writeenable),
    .Imm_writeEnable(framewritecontroller_1_imm_writeenable),
    .ImmSlct_writeEnable(framewritecontroller_1_immslct_writeenable),
    .Unsigned_writeEnable(framewritecontroller_1_unsigned_writeenable),
    .SubEnable_writeEnable(framewritecontroller_1_subenable_writeenable),
    .ResultSelect_writeEnable(framewritecontroller_1_resultselect_writeenable),
    .WriteSelect_writeEnable(framewritecontroller_1_writeselect_writeenable),
    .WriteEnable_writeEnable(framewritecontroller_1_writeenable_writeenable),
    .branchInst_writeEnable(framewritecontroller_1_branchinst_writeenable),
    .branchType_writeEnable(framewritecontroller_1_branchtype_writeenable),
    .jumpInst_writeEnable(framewritecontroller_1_jumpinst_writeenable),
    .load_writeEnable(framewritecontroller_1_load_writeenable),
    .store_writeEnable(framewritecontroller_1_store_writeenable),
    .memlength_writeEnable(framewritecontroller_1_memlength_writeenable),
    .storeData_writeEnable(framewritecontroller_1_storedata_writeenable),
    .auipc_writeEnable(framewritecontroller_1_auipc_writeenable), .clk(clk), .reset(reset),
    .AOp_Out(AOperand_frame), .ALoc_Out(A_Location_frame), .BOp_Out(BOperand_frame),
    .BLoc_Out(B_Location_frame), .Imm_Out(Immediate_frame), .ImmSlct_Out(ImmediateSelect_frame),
    .Unsigned_Out(Unsigned_frame), .SubEnable_Out(SubtractEnable_frame),
    .ResultSelect_Out(resultSelect_frame), .WriteSelect_Out(WriteSelect_frame),
    .WriteEnable_Out(WriteEnable_frame), .pcOverwrite_Out(branchInst_frame),
    .branchType_Out(branchType_frame), .jumpLInk_Out(jumpLink_frame), .jumpRegister_Out(jumpRegister_frame),
    .AOpCompare_Out(AOpCompare_frame), .BOpCompare_Out(BOpCompare_frame), .load_Out(load_frame),
    .loadUnsigned_Out(loadUnsigned), .store_Out(store_frame), .memLength_Out(memLength_frame),
    .storeData_Out(memDataWrite), .auipc_Out(auipcInst_frame));
  or or_2 (or_2_out, auipcInst_frame, jumpLink_frame, branchInst_frame);
  Multiplexer #(.width(32), .enable("false")) multiplexer_3 (
    .in0(A_OpCompare), .in1(PC), .out(A_Operand), .sel(or_2_out));
  or or_3 (or_3_out[0], jumpRegister_frame, jumpLink_frame);
  and and_2 (and_2_out, regWriteEnable, WriteEnable_frame);
  Multiplexer #(.select(2), .width(32), .enable("false")) multiplexer_4 (
    .in0(Result_exec), .in1(PC_next), .in2(memoryDataRead), .out(multiplexer_4_out),
    .sel({load_frame, or_3_out[0]}));  // open: in3
  Adder Adder (.IN_A(AOperand_frame), .IN_B(BOperand_frame), .Subtract(SubtractEnable_frame), .Result(AdderOut));
  Multiplier Multiplier (.IN_A(AOperand_frame), .IN_B(BOperand_frame), .Result(MultiplyOut));
  Divider Divider (
    .IN_A(AOperand_frame), .IN_B(BOperand_frame), .Unsigned(Unsigned_frame), .Result(DivideOut),
    .Remainder(RemainderOut));
  Compare Compare (
    .IN_A(AOpCompare_frame), .IN_B(BOpCompare_frame), .Unsigned(Unsigned_frame), .Greater(GreaterThan),
    .Equal(Equals), .Less(LessThan));
  Registers registers_1 (
    .dataIn(multiplexer_4_out), .writeSelect(WriteSelect_frame), .writeEnable(and_2_out),
    .ReadA_Select(A_Location_frame), .ReadB_Select(B_Location_frame), .clock(clk), .reset(reset),
    .ReadOut_A(A_OpCompare), .ReadOut_B(ReadBData));
  Multiplexer #(.select(3), .width(32), .enable("false")) multiplexer_5 (
    .in0(AdderOut), .in1(MultiplyOut), .in2(DivideOut), .in3(RemainderOut), .in4({{31{1'b0}}, GreaterThan}),
    .in5({{31{1'b0}}, Equals}), .in6({{31{1'b0}}, LessThan}), .out(Result_exec), .sel(resultSelect_frame));  // open: in7
  Multiplexer #(.width(32), .enable("false")) multiplexer_6 (
    .in0(Result_exec), .in1(PC), .out(memAddress), .sel(Writeback_State));
  Multiplexer #(.width(2), .enable("false")) multiplexer_7 (
    .in0(memLength_frame), .in1(2'b11), .out(memLength), .sel(Writeback_State));
  and and_3 (store, store_frame, Execute_State);
  and and_4 (and_4_out, load_frame, Execute_State);
  or or_4 (load, and_4_out, Writeback_State);

  // Other names for the same wires on the sheet: Equals_Padded[0] = Equals; GreaterThan_Padded[0] = GreaterThan;
  //   LessThan_Padded[0] = LessThan; loadUnsigned_frame = loadUnsigned; ReadAData[31:0] = A_OpCompare;
  //   storeData[31:0] = ReadBData; storeData_frame[31:0] = memDataWrite

  // Notes on the sheet:
  //   Input Pin Connections
  //   Control state of pipeline
  //   Control writes to all pipeline memory
  //   Store operands and control signals in an instruction frame
  //   Decode instruction and generate control signals
  //   Arithmetic execution units
  //   Pad comparison results with 0s so that result is 32 bits
  //   General purpose registers
  //   Output Pin Connections
endmodule

module Compare (
  input  [31:0] IN_A,
  input  [31:0] IN_B,
  input  Unsigned,
  output Greater,
  output Equal,
  output Less
);

  wire nor_1_out, or_1_out;
  wire [2:0] comparator_1_gt, comparator_2_gt;

  Comparator #(.width(32)) comparator_1 (
    .a(IN_B), .b(IN_A), .gt(comparator_1_gt[0]), .eq(comparator_1_gt[1]), .lt(comparator_1_gt[2]));
  Comparator #(.width(32)) comparator_2 (
    .a(IN_A), .b(IN_B), .gt(comparator_2_gt[0]), .eq(comparator_2_gt[1]), .lt(comparator_2_gt[2]));
  Multiplexer #(.width(3), .enable("false")) multiplexer_1 (
    .in0(comparator_1_gt), .in1(comparator_2_gt), .out({Less, Equal, Greater}), .sel(or_1_out));
  or or_1 (or_1_out, Unsigned, nor_1_out);
  nor nor_1 (nor_1_out, IN_A[31], IN_B[31]);

  // Other names for the same wires on the sheet: isNegative_a = IN_A[31]; isNegative_b = IN_B[31]
endmodule

module Registers (
  input  [31:0] dataIn,
  input  [4:0] writeSelect,
  input  writeEnable,
  input  [4:0] ReadA_Select,
  input  [4:0] ReadB_Select,
  input  clock,
  input  reset,
  output [31:0] ReadOut_A,
  output [31:0] ReadOut_B
);

  wire and_1_out, and_2_out, and_3_out, and_4_out, and_5_out, and_6_out, and_7_out, and_8_out, and_9_out,
       and_10_out, and_11_out, and_12_out, and_13_out, and_14_out, and_15_out, and_16_out, and_17_out,
       and_18_out, and_19_out, and_20_out, and_21_out, and_22_out, and_23_out, and_24_out, and_25_out,
       and_26_out, and_27_out, and_28_out, and_29_out, and_30_out, and_31_out, r0_select, r1_select,
       r2_select, r3_select, r4_select, r5_select, r6_select, r7_select, r8_select, r9_select, r10_select,
       r11_select, r12_select, r13_select, r14_select, r15_select, r16_select, r17_select, r18_select,
       r19_select, r20_select, r21_select, r22_select, r23_select, r24_select, r25_select, r26_select,
       r27_select, r28_select, r29_select, r30_select, r31_select;
  wire [31:0] r1_dataOut, r2_dataOut, r3_dataOut, r4_dataOut, r5_dataOut, r6_dataOut, r7_dataOut, r8_dataOut,
       r9_dataOut, r10_dataOut, r11_dataOut, r12_dataOut, r13_dataOut, r14_dataOut, r15_dataOut, r16_dataOut,
       r17_dataOut, r18_dataOut, r19_dataOut, r20_dataOut, r21_dataOut, r22_dataOut, r23_dataOut,
       r24_dataOut, r25_dataOut, r26_dataOut, r27_dataOut, r28_dataOut, r29_dataOut, r30_dataOut, r31_dataOut;

  // Probe on {32{1'b0}}
  // Probe on r1_dataOut
  // Probe on r2_dataOut
  // Probe on r3_dataOut
  // Probe on r4_dataOut
  // Probe on r5_dataOut
  // Probe on r6_dataOut
  // Probe on r7_dataOut
  // Probe on r8_dataOut
  // Probe on r9_dataOut
  // Probe on r10_dataOut
  // Probe on r11_dataOut
  // Probe on r12_dataOut
  // Probe on r13_dataOut
  // Probe on r14_dataOut
  // Probe on r15_dataOut
  // Probe on r16_dataOut
  // Probe on r17_dataOut
  // Probe on r18_dataOut
  // Probe on r19_dataOut
  // Probe on r20_dataOut
  // Probe on r21_dataOut
  // Probe on r22_dataOut
  // Probe on r23_dataOut
  // Probe on r24_dataOut
  // Probe on r25_dataOut
  // Probe on r26_dataOut
  // Probe on r27_dataOut
  // Probe on r28_dataOut
  // Probe on r29_dataOut
  // Probe on r30_dataOut
  // Probe on r31_dataOut
  // Probe on {32{1'b0}}
  // Probe on r1_dataOut
  // Probe on r2_dataOut
  // Probe on r3_dataOut
  // Probe on r4_dataOut
  // Probe on r5_dataOut
  // Probe on r6_dataOut
  // Probe on r7_dataOut
  // Probe on r8_dataOut
  // Probe on r9_dataOut
  // Probe on r10_dataOut
  // Probe on r11_dataOut
  // Probe on r12_dataOut
  // Probe on r13_dataOut
  // Probe on r14_dataOut
  // Probe on r15_dataOut
  // Probe on r16_dataOut
  // Probe on r17_dataOut
  // Probe on r18_dataOut
  // Probe on r19_dataOut
  // Probe on r20_dataOut
  // Probe on r21_dataOut
  // Probe on r22_dataOut
  // Probe on r23_dataOut
  // Probe on r24_dataOut
  // Probe on r25_dataOut
  // Probe on r26_dataOut
  // Probe on r27_dataOut
  // Probe on r28_dataOut
  // Probe on r29_dataOut
  // Probe on r30_dataOut
  // Probe on r31_dataOut
  Decoder #(.select(5), .enable("false")) decoder_1 (
    .out0(r0_select), .out1(r1_select), .out2(r2_select), .out3(r3_select), .out4(r4_select),
    .out5(r5_select), .out6(r6_select), .out7(r7_select), .out8(r8_select), .out9(r9_select),
    .out10(r10_select), .out11(r11_select), .out12(r12_select), .out13(r13_select), .out14(r14_select),
    .out15(r15_select), .out16(r16_select), .out17(r17_select), .out18(r18_select), .out19(r19_select),
    .out20(r20_select), .out21(r21_select), .out22(r22_select), .out23(r23_select), .out24(r24_select),
    .out25(r25_select), .out26(r26_select), .out27(r27_select), .out28(r28_select), .out29(r29_select),
    .out30(r30_select), .out31(r31_select), .sel(writeSelect));
  and and_1 (and_1_out, r1_select, writeEnable);
  and and_2 (and_2_out, r2_select, writeEnable);
  and and_3 (and_3_out, r3_select, writeEnable);
  and and_4 (and_4_out, r4_select, writeEnable);
  and and_5 (and_5_out, r5_select, writeEnable);
  and and_6 (and_6_out, r6_select, writeEnable);
  and and_7 (and_7_out, r7_select, writeEnable);
  and and_8 (and_8_out, r8_select, writeEnable);
  and and_9 (and_9_out, r9_select, writeEnable);
  and and_10 (and_10_out, r10_select, writeEnable);
  and and_11 (and_11_out, r11_select, writeEnable);
  and and_12 (and_12_out, r12_select, writeEnable);
  and and_13 (and_13_out, r13_select, writeEnable);
  and and_14 (and_14_out, r14_select, writeEnable);
  and and_15 (and_15_out, r15_select, writeEnable);
  and and_16 (and_16_out, r16_select, writeEnable);
  and and_17 (and_17_out, r17_select, writeEnable);
  and and_18 (and_18_out, r18_select, writeEnable);
  and and_19 (and_19_out, r19_select, writeEnable);
  and and_20 (and_20_out, r20_select, writeEnable);
  and and_21 (and_21_out, r21_select, writeEnable);
  and and_22 (and_22_out, r22_select, writeEnable);
  and and_23 (and_23_out, r23_select, writeEnable);
  and and_24 (and_24_out, r24_select, writeEnable);
  and and_25 (and_25_out, r25_select, writeEnable);
  and and_26 (and_26_out, r26_select, writeEnable);
  and and_27 (and_27_out, r27_select, writeEnable);
  and and_28 (and_28_out, r28_select, writeEnable);
  and and_29 (and_29_out, r29_select, writeEnable);
  and and_30 (and_30_out, r30_select, writeEnable);
  and and_31 (and_31_out, r31_select, writeEnable);
  Register #(.width(32)) r1 (.D(dataIn), .en(and_1_out), .Q(r1_dataOut), .clk(clock), .clr(reset));
  Register #(.width(32)) r2 (.D(dataIn), .en(and_2_out), .Q(r2_dataOut), .clk(clock), .clr(reset));
  Register #(.width(32)) r3 (.D(dataIn), .en(and_3_out), .Q(r3_dataOut), .clk(clock), .clr(reset));
  Register #(.width(32)) r4 (.D(dataIn), .en(and_4_out), .Q(r4_dataOut), .clk(clock), .clr(reset));
  Register #(.width(32)) r5 (.D(dataIn), .en(and_5_out), .Q(r5_dataOut), .clk(clock), .clr(reset));
  Register #(.width(32)) r6 (.D(dataIn), .en(and_6_out), .Q(r6_dataOut), .clk(clock), .clr(reset));
  Register #(.width(32)) r7 (.D(dataIn), .en(and_7_out), .Q(r7_dataOut), .clk(clock), .clr(reset));
  Register #(.width(32)) r8 (.D(dataIn), .en(and_8_out), .Q(r8_dataOut), .clk(clock), .clr(reset));
  Register #(.width(32)) r9 (.D(dataIn), .en(and_9_out), .Q(r9_dataOut), .clk(clock), .clr(reset));
  Register #(.width(32)) r10 (.D(dataIn), .en(and_10_out), .Q(r10_dataOut), .clk(clock), .clr(reset));
  Register #(.width(32)) r11 (.D(dataIn), .en(and_11_out), .Q(r11_dataOut), .clk(clock), .clr(reset));
  Register #(.width(32)) r12 (.D(dataIn), .en(and_12_out), .Q(r12_dataOut), .clk(clock), .clr(reset));
  Register #(.width(32)) r13 (.D(dataIn), .en(and_13_out), .Q(r13_dataOut), .clk(clock), .clr(reset));
  Register #(.width(32)) r14 (.D(dataIn), .en(and_14_out), .Q(r14_dataOut), .clk(clock), .clr(reset));
  Register #(.width(32)) r15 (.D(dataIn), .en(and_15_out), .Q(r15_dataOut), .clk(clock), .clr(reset));
  Register #(.width(32)) r16 (.D(dataIn), .en(and_16_out), .Q(r16_dataOut), .clk(clock), .clr(reset));
  Register #(.width(32)) r17 (.D(dataIn), .en(and_17_out), .Q(r17_dataOut), .clk(clock), .clr(reset));
  Register #(.width(32)) r18 (.D(dataIn), .en(and_18_out), .Q(r18_dataOut), .clk(clock), .clr(reset));
  Register #(.width(32)) r19 (.D(dataIn), .en(and_19_out), .Q(r19_dataOut), .clk(clock), .clr(reset));
  Register #(.width(32)) r20 (.D(dataIn), .en(and_20_out), .Q(r20_dataOut), .clk(clock), .clr(reset));
  Register #(.width(32)) r21 (.D(dataIn), .en(and_21_out), .Q(r21_dataOut), .clk(clock), .clr(reset));
  Register #(.width(32)) r22 (.D(dataIn), .en(and_22_out), .Q(r22_dataOut), .clk(clock), .clr(reset));
  Register #(.width(32)) r23 (.D(dataIn), .en(and_23_out), .Q(r23_dataOut), .clk(clock), .clr(reset));
  Register #(.width(32)) r24 (.D(dataIn), .en(and_24_out), .Q(r24_dataOut), .clk(clock), .clr(reset));
  Register #(.width(32)) r25 (.D(dataIn), .en(and_25_out), .Q(r25_dataOut), .clk(clock), .clr(reset));
  Register #(.width(32)) r26 (.D(dataIn), .en(and_26_out), .Q(r26_dataOut), .clk(clock), .clr(reset));
  Register #(.width(32)) r27 (.D(dataIn), .en(and_27_out), .Q(r27_dataOut), .clk(clock), .clr(reset));
  Register #(.width(32)) r28 (.D(dataIn), .en(and_28_out), .Q(r28_dataOut), .clk(clock), .clr(reset));
  Register #(.width(32)) r29 (.D(dataIn), .en(and_29_out), .Q(r29_dataOut), .clk(clock), .clr(reset));
  Register #(.width(32)) r30 (.D(dataIn), .en(and_30_out), .Q(r30_dataOut), .clk(clock), .clr(reset));
  Register #(.width(32)) r31 (.D(dataIn), .en(and_31_out), .Q(r31_dataOut), .clk(clock), .clr(reset));
  Multiplexer #(.select(5), .width(32), .enable("false")) multiplexer_1 (
    .in0({32{1'b0}}), .in1(r1_dataOut), .in2(r2_dataOut), .in3(r3_dataOut), .in4(r4_dataOut),
    .in5(r5_dataOut), .in6(r6_dataOut), .in7(r7_dataOut), .in8(r8_dataOut), .in9(r9_dataOut),
    .in10(r10_dataOut), .in11(r11_dataOut), .in12(r12_dataOut), .in13(r13_dataOut), .in14(r14_dataOut),
    .in15(r15_dataOut), .in16(r16_dataOut), .in17(r17_dataOut), .in18(r18_dataOut), .in19(r19_dataOut),
    .in20(r20_dataOut), .in21(r21_dataOut), .in22(r22_dataOut), .in23(r23_dataOut), .in24(r24_dataOut),
    .in25(r25_dataOut), .in26(r26_dataOut), .in27(r27_dataOut), .in28(r28_dataOut), .in29(r29_dataOut),
    .in30(r30_dataOut), .in31(r31_dataOut), .out(ReadOut_B), .sel(ReadB_Select));
  Multiplexer #(.select(5), .width(32), .enable("false")) multiplexer_2 (
    .in0({32{1'b0}}), .in1(r1_dataOut), .in2(r2_dataOut), .in3(r3_dataOut), .in4(r4_dataOut),
    .in5(r5_dataOut), .in6(r6_dataOut), .in7(r7_dataOut), .in8(r8_dataOut), .in9(r9_dataOut),
    .in10(r10_dataOut), .in11(r11_dataOut), .in12(r12_dataOut), .in13(r13_dataOut), .in14(r14_dataOut),
    .in15(r15_dataOut), .in16(r16_dataOut), .in17(r17_dataOut), .in18(r18_dataOut), .in19(r19_dataOut),
    .in20(r20_dataOut), .in21(r21_dataOut), .in22(r22_dataOut), .in23(r23_dataOut), .in24(r24_dataOut),
    .in25(r25_dataOut), .in26(r26_dataOut), .in27(r27_dataOut), .in28(r28_dataOut), .in29(r29_dataOut),
    .in30(r30_dataOut), .in31(r31_dataOut), .out(ReadOut_A), .sel(ReadA_Select));

  // Other names for the same wires on the sheet: write_enable = writeEnable

  // Notes on the sheet:
  //   Input Pins
  //   Register Probes
  //   Signed
  //   Unsigned
  //   This decodes the write select input, and determines which register gets written to
  //   Our bank of 32 registers
  //   x0 (register 0) is hardwired to 0 in the RISCV spec (section 2.1)
  //   These muxes determine which register values to output based on read select value
endmodule

module Multiplier (
  input  [31:0] IN_A,
  input  [31:0] IN_B,
  output [31:0] Result
);

  Multiplier_part #(.width(32)) multiplier_1 (.a(IN_A), .b(IN_B), .out(Result), .cin({32{1'b0}}));  // open: cout

  // Notes on the sheet:
  //   AxB
endmodule

module AbsoluteValue (
  input  Unsigned,
  input  [31:0] IN,
  output [31:0] AbsoluteVal,
  output NegativeInput
);

  wire not_1_out;

  not not_1 (not_1_out, Unsigned);
  and and_1 (NegativeInput, not_1_out, IN[31]);
  FlipSign FlipSign (.Flip(NegativeInput), .IN(IN), .Output(AbsoluteVal));

  // Other names for the same wires on the sheet: isNegative = NegativeInput

  // Notes on the sheet:
  //   This circuit takes the absolue value of the input, and outputs if the input was negative
  //   Flip sign if input is negative
  //   <- If the MSB is 1, then the incoming number must be negative
  //   Output absolute value, and sign of the input
endmodule

module FlipSign (
  input  Flip,
  input  [31:0] IN,
  output [31:0] Output
);

  wire [31:0] xor_1_out;

  xor xor_1 (xor_1_out[0], Flip, IN[0]);
  xor xor_2 (xor_1_out[1], Flip, IN[1]);
  xor xor_3 (xor_1_out[2], Flip, IN[2]);
  xor xor_4 (xor_1_out[3], Flip, IN[3]);
  xor xor_5 (xor_1_out[4], Flip, IN[4]);
  xor xor_6 (xor_1_out[5], Flip, IN[5]);
  xor xor_7 (xor_1_out[6], Flip, IN[6]);
  xor xor_8 (xor_1_out[7], Flip, IN[7]);
  xor xor_9 (xor_1_out[8], Flip, IN[8]);
  xor xor_10 (xor_1_out[9], Flip, IN[9]);
  xor xor_11 (xor_1_out[10], Flip, IN[10]);
  xor xor_12 (xor_1_out[11], Flip, IN[11]);
  xor xor_13 (xor_1_out[12], Flip, IN[12]);
  xor xor_14 (xor_1_out[13], Flip, IN[13]);
  xor xor_15 (xor_1_out[14], Flip, IN[14]);
  xor xor_16 (xor_1_out[15], Flip, IN[15]);
  xor xor_17 (xor_1_out[16], Flip, IN[16]);
  xor xor_18 (xor_1_out[17], Flip, IN[17]);
  xor xor_19 (xor_1_out[18], Flip, IN[18]);
  xor xor_20 (xor_1_out[19], Flip, IN[19]);
  xor xor_21 (xor_1_out[20], Flip, IN[20]);
  xor xor_22 (xor_1_out[21], Flip, IN[21]);
  xor xor_23 (xor_1_out[22], Flip, IN[22]);
  xor xor_24 (xor_1_out[23], Flip, IN[23]);
  xor xor_25 (xor_1_out[24], Flip, IN[24]);
  xor xor_26 (xor_1_out[25], Flip, IN[25]);
  xor xor_27 (xor_1_out[26], Flip, IN[26]);
  xor xor_28 (xor_1_out[27], Flip, IN[27]);
  xor xor_29 (xor_1_out[28], Flip, IN[28]);
  xor xor_30 (xor_1_out[29], Flip, IN[29]);
  xor xor_31 (xor_1_out[30], Flip, IN[30]);
  xor xor_32 (xor_1_out[31], Flip, IN[31]);
  Adder_part #(.width(32)) adder_1 (.a(xor_1_out), .b({32{1'b0}}), .out(Output), .cin(Flip));  // open: cout

  // Other names for the same wires on the sheet: b0 = IN[0]; b1 = IN[1]; b2 = IN[2]; b3 = IN[3]; b4 = IN[4];
  //   b5 = IN[5]; b6 = IN[6]; b7 = IN[7]; b8 = IN[8]; b9 = IN[9]; b10 = IN[10]; b11 = IN[11]; b12 = IN[12];
  //   b13 = IN[13]; b14 = IN[14]; b15 = IN[15]; b16 = IN[16]; b17 = IN[17]; b18 = IN[18]; b19 = IN[19]; b20 = IN[20];
  //   b21 = IN[21]; b22 = IN[22]; b23 = IN[23]; b24 = IN[24]; b25 = IN[25]; b26 = IN[26]; b27 = IN[27]; b28 = IN[28];
  //   b29 = IN[29]; b30 = IN[30]; b31 = IN[31]

  // Notes on the sheet:
  //   This circuit flips the sign of the input when "flip" is true, else it remains unchanged
  //   Split 32 bit number into component bits ->
  //   If flip sign is true, flip all the bits
  //   <- Combine all bits into 32 bit bus
  //   Add 1 to flipped bits if flip is true
  //   Output sign flipped value
endmodule

// Instruction Decode
module InstructionDecoder (
  input  [31:0] InstructionIn,
  output [4:0] A_Location,
  output [4:0] B_Location,
  output ImmediateSelect,
  output [31:0] Immediate,
  output Unsigned,
  output SubtractEnable,
  output [4:0] writeSelect,
  output writeEnable,
  output [2:0] resultSelect,
  output error,
  output branchInst,
  output [2:0] branchType,
  output jumpLink,
  output jumpRegister,
  output load,
  output loadUnsigned,
  output store,
  output [1:0] memLength,
  output auipcInst
);

  wire ADD, ADDI, BEQ, BGE, BGEU, BLT, BLTU, BNE, BTYPE, comparator_1_eq, comparator_2_eq, comparator_3_eq,
       comparator_4_eq, comparator_5_eq, comparator_6_eq, comparator_7_eq, comparator_8_eq, comparator_9_eq,
       comparator_10_eq, comparator_11_eq, comparator_12_eq, comparator_13_eq, comparator_14_eq,
       comparator_15_eq, comparator_16_eq, comparator_17_eq, comparator_18_eq, comparator_19_eq,
       comparator_20_eq, comparator_21_eq, comparator_22_eq, comparator_23_eq, comparator_24_eq,
       comparator_25_eq, comparator_26_eq, comparator_27_eq, comparator_28_eq, comparator_29_eq,
       comparator_30_eq, comparator_31_eq, comparator_32_eq, comparator_33_eq, comparator_36_eq,
       comparator_37_eq, comparator_38_eq, comparator_39_eq, comparator_40_eq, comparator_41_eq,
       comparator_42_eq, comparator_43_eq, comparator_44_eq, comparator_45_eq, comparator_46_eq,
       comparator_47_eq, comparator_49_eq, comparator_50_eq, comparator_51_eq, comparator_52_eq, DIV, DIVU,
       LB, LBU, LH, LHU, LUI, LW, MUL, nor_1_out, nor_3_out, or_1_out, or_4_out, or_5_out, or_6_out,
       or_7_out, or_9_out, or_10_out, or_11_out, REM, REMU, SB, SH, SLT, SLTI, SLTIU, SLTU, SW;
  wire [2:0] priority_encoder_1_out;

  Comparator #(.width(7), .mode("unsigned")) comparator_1 (
    .a(InstructionIn[6:0]), .b(7'b0010011), .eq(comparator_1_eq));  // open: gt, lt
  Comparator #(.width(3), .mode("unsigned")) comparator_2 (
    .a(InstructionIn[14:12]), .b(3'b000), .eq(comparator_2_eq));  // open: gt, lt
  Comparator #(.width(7), .mode("unsigned")) comparator_3 (
    .a(InstructionIn[6:0]), .b(7'b0110011), .eq(comparator_3_eq));  // open: gt, lt
  Comparator #(.width(3), .mode("unsigned")) comparator_4 (
    .a(InstructionIn[14:12]), .b(3'b000), .eq(comparator_4_eq));  // open: gt, lt
  Comparator #(.width(7), .mode("unsigned")) comparator_5 (
    .a(InstructionIn[31:25]), .b({7{1'b0}}), .eq(comparator_5_eq));  // open: gt, lt
  Comparator #(.width(7), .mode("unsigned")) comparator_6 (
    .a(InstructionIn[6:0]), .b(7'b0110011), .eq(comparator_6_eq));  // open: gt, lt
  Comparator #(.width(3), .mode("unsigned")) comparator_7 (
    .a(InstructionIn[14:12]), .b(3'b000), .eq(comparator_7_eq));  // open: gt, lt
  Comparator #(.width(7), .mode("unsigned")) comparator_8 (
    .a(InstructionIn[31:25]), .b(7'b0100000), .eq(comparator_8_eq));  // open: gt, lt
  Comparator #(.width(7), .mode("unsigned")) comparator_9 (
    .a(InstructionIn[6:0]), .b(7'b0110011), .eq(comparator_9_eq));  // open: gt, lt
  Comparator #(.width(3), .mode("unsigned")) comparator_10 (
    .a(InstructionIn[14:12]), .b(3'b000), .eq(comparator_10_eq));  // open: gt, lt
  Comparator #(.width(7), .mode("unsigned")) comparator_11 (
    .a(InstructionIn[31:25]), .b(7'b0000001), .eq(comparator_11_eq));  // open: gt, lt
  Comparator #(.width(7), .mode("unsigned")) comparator_12 (
    .a(InstructionIn[6:0]), .b(7'b0110011), .eq(comparator_12_eq));  // open: gt, lt
  Comparator #(.width(3), .mode("unsigned")) comparator_13 (
    .a(InstructionIn[14:12]), .b(3'b100), .eq(comparator_13_eq));  // open: gt, lt
  Comparator #(.width(7), .mode("unsigned")) comparator_14 (
    .a(InstructionIn[31:25]), .b(7'b0000001), .eq(comparator_14_eq));  // open: gt, lt
  Comparator #(.width(7), .mode("unsigned")) comparator_15 (
    .a(InstructionIn[6:0]), .b(7'b0110011), .eq(comparator_15_eq));  // open: gt, lt
  Comparator #(.width(3), .mode("unsigned")) comparator_16 (
    .a(InstructionIn[14:12]), .b(3'b101), .eq(comparator_16_eq));  // open: gt, lt
  Comparator #(.width(7), .mode("unsigned")) comparator_17 (
    .a(InstructionIn[31:25]), .b(7'b0000001), .eq(comparator_17_eq));  // open: gt, lt
  Comparator #(.width(7), .mode("unsigned")) comparator_18 (
    .a(InstructionIn[6:0]), .b(7'b0110011), .eq(comparator_18_eq));  // open: gt, lt
  Comparator #(.width(3), .mode("unsigned")) comparator_19 (
    .a(InstructionIn[14:12]), .b(3'b110), .eq(comparator_19_eq));  // open: gt, lt
  Comparator #(.width(7), .mode("unsigned")) comparator_20 (
    .a(InstructionIn[31:25]), .b(7'b0000001), .eq(comparator_20_eq));  // open: gt, lt
  Comparator #(.width(7), .mode("unsigned")) comparator_21 (
    .a(InstructionIn[6:0]), .b(7'b0110011), .eq(comparator_21_eq));  // open: gt, lt
  Comparator #(.width(3), .mode("unsigned")) comparator_22 (
    .a(InstructionIn[14:12]), .b(3'b111), .eq(comparator_22_eq));  // open: gt, lt
  Comparator #(.width(7), .mode("unsigned")) comparator_23 (
    .a(InstructionIn[31:25]), .b(7'b0000001), .eq(comparator_23_eq));  // open: gt, lt
  Comparator #(.width(7), .mode("unsigned")) comparator_24 (
    .a(InstructionIn[6:0]), .b(7'b0010011), .eq(comparator_24_eq));  // open: gt, lt
  Comparator #(.width(3), .mode("unsigned")) comparator_25 (
    .a(InstructionIn[14:12]), .b(3'b010), .eq(comparator_25_eq));  // open: gt, lt
  Comparator #(.width(7), .mode("unsigned")) comparator_26 (
    .a(InstructionIn[6:0]), .b(7'b0010011), .eq(comparator_26_eq));  // open: gt, lt
  Comparator #(.width(3), .mode("unsigned")) comparator_27 (
    .a(InstructionIn[14:12]), .b(3'b011), .eq(comparator_27_eq));  // open: gt, lt
  Comparator #(.width(7), .mode("unsigned")) comparator_28 (
    .a(InstructionIn[6:0]), .b(7'b0110011), .eq(comparator_28_eq));  // open: gt, lt
  Comparator #(.width(3), .mode("unsigned")) comparator_29 (
    .a(InstructionIn[14:12]), .b(3'b010), .eq(comparator_29_eq));  // open: gt, lt
  Comparator #(.width(7), .mode("unsigned")) comparator_30 (
    .a(InstructionIn[31:25]), .b({7{1'b0}}), .eq(comparator_30_eq));  // open: gt, lt
  Comparator #(.width(7), .mode("unsigned")) comparator_31 (
    .a(InstructionIn[6:0]), .b(7'b0110011), .eq(comparator_31_eq));  // open: gt, lt
  Comparator #(.width(3), .mode("unsigned")) comparator_32 (
    .a(InstructionIn[14:12]), .b(3'b011), .eq(comparator_32_eq));  // open: gt, lt
  Comparator #(.width(7), .mode("unsigned")) comparator_33 (
    .a(InstructionIn[31:25]), .b({7{1'b0}}), .eq(comparator_33_eq));  // open: gt, lt
  Comparator #(.width(7), .mode("unsigned")) comparator_34 (
    .a(InstructionIn[6:0]), .b(7'b1101111), .eq(jumpLink));  // open: gt, lt
  Comparator #(.width(7), .mode("unsigned")) comparator_35 (
    .a(InstructionIn[6:0]), .b(7'b1100111), .eq(jumpRegister));  // open: gt, lt
  Comparator #(.width(7), .mode("unsigned")) comparator_36 (
    .a(InstructionIn[6:0]), .b(7'b1100011), .eq(comparator_36_eq));  // open: gt, lt
  Comparator #(.width(3), .mode("unsigned")) comparator_37 (
    .a(InstructionIn[14:12]), .b(3'b000), .eq(comparator_37_eq));  // open: gt, lt
  Comparator #(.width(7), .mode("unsigned")) comparator_38 (
    .a(InstructionIn[6:0]), .b(7'b1100011), .eq(comparator_38_eq));  // open: gt, lt
  Comparator #(.width(3), .mode("unsigned")) comparator_39 (
    .a(InstructionIn[14:12]), .b(3'b001), .eq(comparator_39_eq));  // open: gt, lt
  Comparator #(.width(7), .mode("unsigned")) comparator_40 (
    .a(InstructionIn[6:0]), .b(7'b1100011), .eq(comparator_40_eq));  // open: gt, lt
  Comparator #(.width(3), .mode("unsigned")) comparator_41 (
    .a(InstructionIn[14:12]), .b(3'b100), .eq(comparator_41_eq));  // open: gt, lt
  Comparator #(.width(7), .mode("unsigned")) comparator_42 (
    .a(InstructionIn[6:0]), .b(7'b1100011), .eq(comparator_42_eq));  // open: gt, lt
  Comparator #(.width(3), .mode("unsigned")) comparator_43 (
    .a(InstructionIn[14:12]), .b(3'b101), .eq(comparator_43_eq));  // open: gt, lt
  Comparator #(.width(7), .mode("unsigned")) comparator_44 (
    .a(InstructionIn[6:0]), .b(7'b1100011), .eq(comparator_44_eq));  // open: gt, lt
  Comparator #(.width(3), .mode("unsigned")) comparator_45 (
    .a(InstructionIn[14:12]), .b(3'b110), .eq(comparator_45_eq));  // open: gt, lt
  Comparator #(.width(7), .mode("unsigned")) comparator_46 (
    .a(InstructionIn[6:0]), .b(7'b1100011), .eq(comparator_46_eq));  // open: gt, lt
  Comparator #(.width(3), .mode("unsigned")) comparator_47 (
    .a(InstructionIn[14:12]), .b(3'b111), .eq(comparator_47_eq));  // open: gt, lt
  Comparator #(.width(7), .mode("unsigned")) comparator_48 (
    .a(InstructionIn[6:0]), .b(7'b0000011), .eq(load));  // open: gt, lt
  Comparator #(.width(7), .mode("unsigned")) comparator_49 (
    .a(InstructionIn[6:0]), .b(7'b0000011), .eq(comparator_49_eq));  // open: gt, lt
  Comparator #(.width(3), .mode("unsigned")) comparator_50 (
    .a(InstructionIn[14:12]), .b(3'b100), .eq(comparator_50_eq));  // open: gt, lt
  Comparator #(.width(7), .mode("unsigned")) comparator_51 (
    .a(InstructionIn[6:0]), .b(7'b0000011), .eq(comparator_51_eq));  // open: gt, lt
  Comparator #(.width(3), .mode("unsigned")) comparator_52 (
    .a(InstructionIn[14:12]), .b(3'b101), .eq(comparator_52_eq));  // open: gt, lt
  Comparator #(.width(3), .mode("unsigned")) comparator_53 (
    .a(InstructionIn[14:12]), .b(3'b000), .eq(LB));  // open: gt, lt
  Comparator #(.width(3), .mode("unsigned")) comparator_54 (
    .a(InstructionIn[14:12]), .b(3'b001), .eq(LH));  // open: gt, lt
  Comparator #(.width(3), .mode("unsigned")) comparator_55 (
    .a(InstructionIn[14:12]), .b(3'b010), .eq(LW));  // open: gt, lt
  Comparator #(.width(7), .mode("unsigned")) comparator_56 (
    .a(InstructionIn[6:0]), .b(7'b0100011), .eq(store));  // open: gt, lt
  Comparator #(.width(3), .mode("unsigned")) comparator_57 (
    .a(InstructionIn[14:12]), .b(3'b000), .eq(SB));  // open: gt, lt
  Comparator #(.width(3), .mode("unsigned")) comparator_58 (
    .a(InstructionIn[14:12]), .b(3'b001), .eq(SH));  // open: gt, lt
  Comparator #(.width(3), .mode("unsigned")) comparator_59 (
    .a(InstructionIn[14:12]), .b(3'b010), .eq(SW));  // open: gt, lt
  Comparator #(.width(7), .mode("unsigned")) comparator_60 (
    .a(InstructionIn[6:0]), .b(7'b0110111), .eq(LUI));  // open: gt, lt
  Comparator #(.width(7), .mode("unsigned")) comparator_61 (
    .a(InstructionIn[6:0]), .b(7'b0010111), .eq(auipcInst));  // open: gt, lt
  and and_1 (ADDI, comparator_1_eq, comparator_2_eq);
  and and_2 (ADD, comparator_3_eq, comparator_4_eq, comparator_5_eq);
  and and_3 (SubtractEnable, comparator_6_eq, comparator_7_eq, comparator_8_eq);
  and and_4 (MUL, comparator_9_eq, comparator_10_eq, comparator_11_eq);
  and and_5 (DIV, comparator_12_eq, comparator_13_eq, comparator_14_eq);
  and and_6 (DIVU, comparator_15_eq, comparator_16_eq, comparator_17_eq);
  and and_7 (REM, comparator_18_eq, comparator_19_eq, comparator_20_eq);
  and and_8 (REMU, comparator_21_eq, comparator_22_eq, comparator_23_eq);
  and and_9 (SLTI, comparator_24_eq, comparator_25_eq);
  and and_10 (SLTIU, comparator_26_eq, comparator_27_eq);
  and and_11 (SLT, comparator_28_eq, comparator_29_eq, comparator_30_eq);
  and and_12 (SLTU, comparator_31_eq, comparator_32_eq, comparator_33_eq);
  and and_13 (BEQ, comparator_36_eq, comparator_37_eq);
  and and_14 (BNE, comparator_38_eq, comparator_39_eq);
  and and_15 (BLT, comparator_40_eq, comparator_41_eq);
  and and_16 (BGE, comparator_42_eq, comparator_43_eq);
  and and_17 (BLTU, comparator_44_eq, comparator_45_eq);
  and and_18 (BGEU, comparator_46_eq, comparator_47_eq);
  and and_19 (LBU, comparator_49_eq, comparator_50_eq);
  and and_20 (LHU, comparator_51_eq, comparator_52_eq);
  Multiplexer #(.width(5), .enable("false")) multiplexer_1 (
    .in0(InstructionIn[19:15]), .in1({5{1'b0}}), .out(A_Location), .sel(LUI));
  or or_1 (or_1_out, LUI, auipcInst);
  or or_2 (ImmediateSelect, ADDI, SLTI, SLTIU, jumpLink, BTYPE, load, store, jumpRegister, LUI, auipcInst);
  Comparator #(.width(7), .mode("unsigned")) comparator_62 (
    .a(InstructionIn[6:0]), .b(7'b1100011), .eq(BTYPE));  // open: gt, lt
  Multiplexer #(.select(3), .width(32), .enable("false")) multiplexer_2 (
    .in0({{21{InstructionIn[31]}}, InstructionIn[30:20]}),
    .in1({{12{InstructionIn[31]}}, InstructionIn[19:12], InstructionIn[20], InstructionIn[30:21], 1'b0}),
    .in2({{20{InstructionIn[31]}}, InstructionIn[7], InstructionIn[30:25], InstructionIn[11:8], 1'b0}),
    .in3({{21{InstructionIn[31]}}, InstructionIn[30:25], InstructionIn[11:7]}),
    .in4({InstructionIn[31:12], {12{1'b0}}}), .out(Immediate), .sel(priority_encoder_1_out));  // open: in5, in6, in7
  nor nor_1 (nor_1_out, auipcInst, LUI, jumpLink, BTYPE, store);
  or or_3 (Unsigned, DIVU, REMU, SLTIU, SLTU, BLTU, BGEU);
  nor nor_2 (writeEnable, BTYPE, store);
  or or_4 (or_4_out, load, store, BTYPE, jumpLink, jumpRegister, ADDI, ADD, SubtractEnable, LUI, auipcInst);
  or or_5 (or_5_out, DIV, DIVU);
  or or_6 (or_6_out, REM, REMU);
  or or_7 (or_7_out, SLTI, SLTIU, SLT, SLTU);
  Comparator #(.width(7), .mode("unsigned")) comparator_63 (
    .a(InstructionIn[6:0]), .b(7'b1100011), .eq(branchInst));  // open: gt, lt
  nor nor_3 (nor_3_out, BEQ, BNE, BLT, BGE, BLTU, BGEU);
  or or_8 (loadUnsigned, LBU, LHU);
  or or_9 (or_9_out, LBU, LB, SB);
  or or_10 (or_10_out, LHU, LH, SH);
  or or_11 (or_11_out, LW, SW);
  Priority_Encoder priority_encoder_1 (
    .in0(nor_1_out), .in1(jumpLink), .in2(BTYPE), .in3(store), .in4(or_1_out), .in5(1'b0), .in6(1'b0),
    .in7(1'b0), .out(priority_encoder_1_out), .en_in(1'b1));  // open: gs, en_out
  Priority_Encoder #(.disabled(0)) priority_encoder_2 (
    .in0(or_4_out), .in1(MUL), .in2(or_5_out), .in3(or_6_out), .in4(1'b0), .in5(1'b0), .in6(or_7_out),
    .in7(1'b0), .out(resultSelect), .en_in(1'b1), .en_out(error));  // open: gs
  Priority_Encoder #(.disabled(0)) priority_encoder_3 (
    .in0(nor_3_out), .in1(BEQ), .in2(BNE), .in3(BLT), .in4(BGE), .in5(BLTU), .in6(BGEU), .in7(1'b0),
    .out(branchType), .en_in(1'b1));  // open: gs, en_out
  Priority_Encoder #(.select(2), .disabled(0)) priority_encoder_4 (
    .in0(or_9_out), .in1(or_10_out), .in2(1'b0), .in3(or_11_out), .out(memLength), .en_in(1'b1));  // open: gs, en_out
  // Probe on Immediate

  assign B_Location = InstructionIn[24:20];
  assign writeSelect = InstructionIn[11:7];

  // Other names for the same wires on the sheet: AUIPC = auipcInst; im_11 = InstructionIn[7];
  //   imm_4_0[4:0] = InstructionIn[11:7];
  //   immext_btype[31:1] = {{20{InstructionIn[31]}}, InstructionIn[7], InstructionIn[30:25], InstructionIn[11:8]};
  //   immext_stype[31:0] = {{21{InstructionIn[31]}}, InstructionIn[30:25], InstructionIn[11:7]};
  //   rd[4:0] = InstructionIn[11:7]; imm_4_1[3:0] = InstructionIn[11:8]; funct3[2:0] = InstructionIn[14:12];
  //   imm_19_12[7:0] = InstructionIn[19:12]; imm_31_12[19:0] = InstructionIn[31:12];
  //   immext_jtype[31:1] = {{12{InstructionIn[31]}}, InstructionIn[19:12], InstructionIn[20], InstructionIn[30:21]};
  //   immext_utype[31:12] = InstructionIn[31:12]; rs1[4:0] = InstructionIn[19:15]; imm_11 = InstructionIn[20];
  //   imm_11_0[11:0] = InstructionIn[31:20]; immext_itype[31:0] = {{21{InstructionIn[31]}}, InstructionIn[30:20]};
  //   rs2[4:0] = InstructionIn[24:20]; imm_10_1[9:0] = InstructionIn[30:21]; funct7[6:0] = InstructionIn[31:25];
  //   imm_10_5[5:0] = InstructionIn[30:25]; imm_11_5[6:0] = InstructionIn[31:25]; im_12 = InstructionIn[31];
  //   imm_20 = InstructionIn[31]; opcode[6:0] = InstructionIn[6:0]; JAL = jumpLink; JALR = jumpRegister;
  //   SUB = SubtractEnable; UnsupportedInstruction = error

  // Notes on the sheet:
  //   Opcodes
  //   funct3
  //   Hardcoded values of supported opcodes and functions
  //   Split instruction into component parts for all 6 possible format types (spec sec2.3)
  //   R type
  //   I type
  //   S type
  //   B type
  //   U type
  //   J type
  //   funct7
  //   We don't need to check opcodes here since we only care about the width value ->
  //   Check for and parse supported instructions
  //   GreaterThan currently unused
  //   Sign extend immediate input
  //   Equals currently unused
  //   Extra unused option
  //   Produce output control signals based on instruction
  //   Encode branch type
  //   Encode resultSelect signal
  //   OutputPins
endmodule

// Instruction Frame
module InstructionFrame (
  input  [31:0] AOp_In,
  input  [4:0] ALoc_In,
  input  [31:0] BOp_In,
  input  [4:0] BLoc_In,
  input  [31:0] Imm_In,
  input  ImmSlct_In,
  input  Unsigned_In,
  input  SubEnable_In,
  input  [2:0] ResultSelect_In,
  input  [4:0] WriteSelect_In,
  input  WriteEnable_In,
  input  branchInst_In,
  input  [2:0] branchType_In,
  input  jumpLink_In,
  input  jumpRegister_In,
  input  [31:0] aOpCompare_in,
  input  [31:0] bOpCompare_in,
  input  load_In,
  input  loadUnsigned_In,
  input  store_In,
  input  [1:0] memLength_In,
  input  [31:0] storeData_in,
  input  auipc_In,
  input  AOp_writeEnable,
  input  ALoc_writeEnable,
  input  BOp_writeEnable,
  input  BLoc_writeEnable,
  input  Imm_writeEnable,
  input  ImmSlct_writeEnable,
  input  Unsigned_writeEnable,
  input  SubEnable_writeEnable,
  input  ResultSelect_writeEnable,
  input  WriteSelect_writeEnable,
  input  WriteEnable_writeEnable,
  input  branchInst_writeEnable,
  input  branchType_writeEnable,
  input  jumpInst_writeEnable,
  input  load_writeEnable,
  input  store_writeEnable,
  input  memlength_writeEnable,
  input  storeData_writeEnable,
  input  auipc_writeEnable,
  input  clk,
  input  reset,
  output [31:0] AOp_Out,
  output [4:0] ALoc_Out,
  output [31:0] BOp_Out,
  output [4:0] BLoc_Out,
  output [31:0] Imm_Out,
  output ImmSlct_Out,
  output Unsigned_Out,
  output SubEnable_Out,
  output [2:0] ResultSelect_Out,
  output [4:0] WriteSelect_Out,
  output WriteEnable_Out,
  output pcOverwrite_Out,
  output [2:0] branchType_Out,
  output jumpLInk_Out,
  output jumpRegister_Out,
  output [31:0] AOpCompare_Out,
  output [31:0] BOpCompare_Out,
  output load_Out,
  output loadUnsigned_Out,
  output store_Out,
  output [1:0] memLength_Out,
  output [31:0] storeData_Out,
  output auipc_Out
);

  wire pcOverwrite_we;

  Register #(.width(32)) A_Operand (.D(AOp_In), .en(AOp_writeEnable), .Q(AOp_Out), .clk(clk), .clr(reset));
  Register #(.width(32)) B_Operand (.D(BOp_In), .en(BOp_writeEnable), .Q(BOp_Out), .clk(clk), .clr(reset));
  Register #(.width(32)) Immediate (.D(Imm_In), .en(Imm_writeEnable), .Q(Imm_Out), .clk(clk), .clr(reset));
  Register #(.width(1)) Unsigned (.D(Unsigned_In), .en(Unsigned_writeEnable), .Q(Unsigned_Out), .clk(clk), .clr(reset));
  Register #(.width(3)) ResultSelect (
    .D(ResultSelect_In), .en(ResultSelect_writeEnable), .Q(ResultSelect_Out), .clk(clk), .clr(reset));
  Register #(.width(5)) WriteSelect (
    .D(WriteSelect_In), .en(WriteSelect_writeEnable), .Q(WriteSelect_Out), .clk(clk), .clr(reset));
  Register #(.width(1)) jumpLink (.D(jumpLink_In), .en(jumpInst_writeEnable), .Q(jumpLInk_Out), .clk(clk), .clr(reset));
  Register #(.width(32)) A_OpCompare (
    .D(aOpCompare_in), .en(AOp_writeEnable), .Q(AOpCompare_Out), .clk(clk), .clr(reset));
  Register #(.width(32)) B_OpCompare (
    .D(bOpCompare_in), .en(BOp_writeEnable), .Q(BOpCompare_Out), .clk(clk), .clr(reset));
  Register #(.width(1)) Load (.D(load_In), .en(load_writeEnable), .Q(load_Out), .clk(clk), .clr(reset));
  Register #(.width(1)) Store (.D(store_In), .en(store_writeEnable), .Q(store_Out), .clk(clk), .clr(reset));
  Register #(.width(1)) Auipc (.D(auipc_In), .en(auipc_writeEnable), .Q(auipc_Out), .clk(clk), .clr(reset));
  Register #(.width(5)) A_Location (.D(ALoc_In), .en(ALoc_writeEnable), .Q(ALoc_Out), .clk(clk), .clr(reset));
  Register #(.width(5)) B_Location (.D(BLoc_In), .en(BLoc_writeEnable), .Q(BLoc_Out), .clk(clk), .clr(reset));
  Register #(.width(1)) ImmediateSelect (
    .D(ImmSlct_In), .en(ImmSlct_writeEnable), .Q(ImmSlct_Out), .clk(clk), .clr(reset));
  Register #(.width(1)) SubtractEnable (
    .D(SubEnable_In), .en(SubEnable_writeEnable), .Q(SubEnable_Out), .clk(clk), .clr(reset));
  Register #(.width(1)) branchInst (
    .D(branchInst_In), .en(pcOverwrite_we), .Q(pcOverwrite_Out), .clk(clk), .clr(reset));
  Register #(.width(1)) WriteEnable (
    .D(WriteEnable_In), .en(WriteEnable_writeEnable), .Q(WriteEnable_Out), .clk(clk), .clr(reset));
  Register #(.width(1)) jumpRegister (
    .D(jumpRegister_In), .en(jumpInst_writeEnable), .Q(jumpRegister_Out), .clk(clk), .clr(reset));
  Register #(.width(3)) branchType (
    .D(branchType_In), .en(branchType_writeEnable), .Q(branchType_Out), .clk(clk), .clr(reset));
  Register #(.width(2)) MemLength (
    .D(memLength_In), .en(memlength_writeEnable), .Q(memLength_Out), .clk(clk), .clr(reset));
  Register #(.width(1)) LoadUnsigned (
    .D(loadUnsigned_In), .en(load_writeEnable), .Q(loadUnsigned_Out), .clk(clk), .clr(reset));
  Register #(.width(32)) StoreData (
    .D(storeData_in), .en(storeData_writeEnable), .Q(storeData_Out), .clk(clk), .clr(reset));

  // Other names for the same wires on the sheet: ALoc_we = ALoc_writeEnable; AOp_we = AOp_writeEnable;
  //   auipc_we = auipc_writeEnable; BLoc_we = BLoc_writeEnable; BOp_we = BOp_writeEnable;
  //   branchInst_Out = pcOverwrite_Out; branchInst_we = branchInst_writeEnable;
  //   branchType_we = branchType_writeEnable; Imm_we = Imm_writeEnable; ImmSlct_we = ImmSlct_writeEnable;
  //   jumpInst_we = jumpInst_writeEnable; load_we = load_writeEnable; memLength_we = memlength_writeEnable;
  //   ResultSelect_we = ResultSelect_writeEnable; rst = reset; store_we = store_writeEnable;
  //   storeData_we = storeData_writeEnable; SubEnable_we = SubEnable_writeEnable; Unsigned_we = Unsigned_writeEnable;
  //   WreteSelect_In[4:0] = WriteSelect_In; WreteSelect_Out[4:0] = WriteSelect_Out;
  //   WriteEnable_we = WriteEnable_writeEnable; WriteSelect_we = WriteSelect_writeEnable

  // Notes on the sheet:
  //   Input Pin Connections
  //   Data In
  //   Write Emable In
  //   Clock and Reset
  //   Frame Data Registers
  //   Output Pin Connections
  //   Data Out
endmodule

// WriteController
module FrameWriteController (
  input  FetchRequest_State,
  input  FetchReceive_State,
  input  Decode_State,
  input  Setup_State,
  input  Execute_State,
  input  memRead_State,
  input  Writeback_State,
  output AOp_writeEnable,
  output ALoc_writeEnable,
  output BOp_writeEnable,
  output BLoc_writeEnable,
  output Imm_writeEnable,
  output ImmSlct_writeEnable,
  output Unsigned_writeEnable,
  output SubEnable_writeEnable,
  output ResultSelect_writeEnable,
  output WriteSelect_writeEnable,
  output WriteEnable_writeEnable,
  output Result_writeEnable,
  output cir_writeEnable,
  output pc_writeEnable,
  output branchInst_writeEnable,
  output branchType_writeEnable,
  output jumpInst_writeEnable,
  output load_writeEnable,
  output store_writeEnable,
  output memLength_writeEnable,
  output storeData_writeEnable,
  output auipc_writeEnable
);

  or or_1 (Result_writeEnable, Execute_State, memRead_State);

  assign ALoc_writeEnable = Decode_State;
  assign AOp_writeEnable = Setup_State;
  assign auipc_writeEnable = Decode_State;
  assign BLoc_writeEnable = Decode_State;
  assign BOp_writeEnable = Setup_State;
  assign branchInst_writeEnable = Decode_State;
  assign branchType_writeEnable = Decode_State;
  assign cir_writeEnable = FetchReceive_State;
  assign Imm_writeEnable = Decode_State;
  assign ImmSlct_writeEnable = Decode_State;
  assign jumpInst_writeEnable = Decode_State;
  assign load_writeEnable = Decode_State;
  assign memLength_writeEnable = Decode_State;
  assign pc_writeEnable = Execute_State;
  assign ResultSelect_writeEnable = Decode_State;
  assign store_writeEnable = Decode_State;
  assign storeData_writeEnable = Setup_State;
  assign SubEnable_writeEnable = Decode_State;
  assign Unsigned_writeEnable = Decode_State;
  assign WriteEnable_writeEnable = Decode_State;
  assign WriteSelect_writeEnable = Decode_State;

  // Other names for the same wires on the sheet: cir_we = FetchReceive_State; pc_we = Execute_State;
  //   Result_we = Result_writeEnable; ALoc_we = Decode_State; auipc_we = Decode_State; BLoc_we = Decode_State;
  //   branchInst_we = Decode_State; branchType_we = Decode_State; Imm_we = Decode_State; ImmSlct_we = Decode_State;
  //   jumpInst_we = Decode_State; load_we = Decode_State; memLength_we = Decode_State; ResultSelect_we = Decode_State;
  //   store_we = Decode_State; SubEnable_we = Decode_State; Unsigned_we = Decode_State; WreteSelect_we = Decode_State;
  //   WriteEnable_we = Decode_State; AOp_we = Setup_State; BOp_we = Setup_State; storeData_we = Setup_State

  // Notes on the sheet:
  //   Input Pin Connections
  //   Determine Write Enables on Current Pipeline State
  //   Output pin connections
  //   Write Emable Out
endmodule

module PipelineStateController (
  input  loadInst,
  input  clk,
  input  reset,
  output FetchRequest_State,
  output Fetch_State,
  output Decode_State,
  output Setup_State,
  output Execute_State,
  output memRead_State,
  output Writeback_State
);

  wire and_1_out, or_1_out;
  wire [2:0] adder_1_out, nextPipelineState, PipelineState;

  Register #(.width(3)) PipeplineState (.D(nextPipelineState), .en(1'b1), .Q(PipelineState), .clk(clk), .clr(reset));
  Adder_part #(.width(3)) adder_1 (.a(PipelineState), .b(3'b001), .out(adder_1_out), .cin(1'b0));  // open: cout
  and and_1 (and_1_out, Execute_State, ~loadInst);  // AND_Gate
  Multiplexer #(.width(3), .enable("false")) multiplexer_1 (
    .in0(adder_1_out), .in1(3'b000), .out(nextPipelineState), .sel(or_1_out));
  or or_1 (or_1_out, and_1_out, memRead_State);
  Decoder #(.select(3), .enable("false")) decoder_1 (
    .out0(Writeback_State), .out1(FetchRequest_State), .out2(Fetch_State), .out3(Decode_State),
    .out4(Setup_State), .out5(Execute_State), .out6(memRead_State), .sel(PipelineState));  // open: out7

  // Other names for the same wires on the sheet: FetchReceive_State = Fetch_State

  // Notes on the sheet:
  //   Input Pin Connections
  //   Increment pipeline state
  //   Reset state when state=6
  //   Decode pipeline states
  //   Output Pin Connections
endmodule

module pc_instFetch_Controller (
  input  [31:0] MemoryIn,
  input  cir_we,
  input  [31:0] pcOverwrite,
  input  pc_we,
  input  [2:0] branchType,
  input  jumpInst,
  input  compare_greater,
  input  compare_equals,
  input  compare_less,
  input  clk,
  input  reset,
  output [31:0] InstructionOut,
  output [31:0] PC,
  output [31:0] PC_next
);

  wire and_1_out, and_2_out, and_3_out, and_4_out, and_5_out, and_6_out, BEQ, BGE, BGEU, BLT, BLTU, BNE,
       pcOverwrite_en;
  wire [31:0] multiplexer_1_out;

  Multiplexer #(.width(32), .enable("false")) multiplexer_1 (
    .in0(PC_next), .in1(pcOverwrite), .out(multiplexer_1_out), .sel(pcOverwrite_en));
  Register #(.width(32)) u_PC (.D(multiplexer_1_out), .en(pc_we), .Q(PC), .clk(clk), .clr(reset));
  Register #(.width(32)) CIR (.D(MemoryIn), .en(cir_we), .Q(InstructionOut), .clk(clk), .clr(reset));
  Decoder #(.select(3), .enable("false")) decoder_1 (
    .out1(BEQ), .out2(BNE), .out3(BLT), .out4(BGE), .out5(BLTU), .out6(BGEU), .sel(branchType));  // open: out0, out7
  Adder_part #(.width(32)) adder_1 (.a(PC), .b(32'h4), .out(PC_next), .cin(1'b0));  // open: cout
  and and_1 (and_1_out, BEQ, compare_equals);
  and and_2 (and_2_out, BNE, ~compare_equals);  // AND_Gate
  and and_3 (and_3_out, BLT, compare_less);
  and and_4 (and_4_out, BGE, compare_greater);
  and and_5 (and_5_out, BLTU, compare_less);
  and and_6 (and_6_out, BGEU, compare_greater);
  or or_1 (pcOverwrite_en, jumpInst, and_1_out, and_2_out, and_3_out, and_4_out, and_5_out, and_6_out);

  // Notes on the sheet:
  //   Input Pin Connections
  //   Current Instruction Register (CIR)
  //   Increment Program Counter (PC) after each instruction, unless it is overwritten
  //   Determine if we should overwrite PC for control flow instructions
  //   Output Pin Connections
endmodule

module MainMemory (
  input  [31:0] addressIn,
  input  [31:0] dataIn,
  input  [3:0] byteSelect,
  input  store,
  input  load,
  input  clk,
  input  reset,
  output [31:0] dataOut,
  output addressOutOfRange
);

  wire comparator_1_eq, not_1_out, or_1_out;
  wire [31:0] memIn;

  // Probe on addressIn
  // Probe on dataIn
  Comparator #(.width(6)) comparator_1 (.a(addressIn[31:26]), .b({6{1'b0}}), .eq(comparator_1_eq));  // open: gt, lt
  not not_1 (not_1_out, comparator_1_eq);
  or or_1 (or_1_out, load, store);
  and and_1 (addressOutOfRange, not_1_out, or_1_out);
  RAM #(.addrWidth(24), .dataWidth(32), .bus("separate")) ram_1 (
    .addr(addressIn[25:2]), .din(memIn), .data(dataOut), .str(store), .sel(1'b1), .clk(clk), .ld(1'b1));  // open: clr
  Multiplexer #(.width(8), .enable("false")) multiplexer_1 (
    .in0(dataOut[7:0]), .in1(dataIn[7:0]), .out(memIn[7:0]), .sel(byteSelect[0]));
  Multiplexer #(.width(8), .enable("false")) multiplexer_2 (
    .in0(dataOut[15:8]), .in1(dataIn[15:8]), .out(memIn[15:8]), .sel(byteSelect[1]));
  Multiplexer #(.width(8), .enable("false")) multiplexer_3 (
    .in0(dataOut[23:16]), .in1(dataIn[23:16]), .out(memIn[23:16]), .sel(byteSelect[2]));
  Multiplexer #(.width(8), .enable("false")) multiplexer_4 (
    .in0(dataOut[31:24]), .in1(dataIn[31:24]), .out(memIn[31:24]), .sel(byteSelect[3]));
  // Probe on dataOut

  // Other names for the same wires on the sheet: addresIn[31:0] = addressIn; addresLower[1:0] = addressIn[1:0];
  //   B0_write = byteSelect[0]; B1_write = byteSelect[1]; B2_write = byteSelect[2]; B3_write = byteSelect[3];
  //   input_byte0[7:0] = dataIn[7:0]; input_byte1[7:0] = dataIn[15:8]; input_byte2[7:0] = dataIn[23:16];
  //   input_byte3[7:0] = dataIn[31:24]; memCurrent_byte0[7:0] = dataOut[7:0]; memCurrent_byte1[7:0] = dataOut[15:8];
  //   memCurrent_byte2[7:0] = dataOut[23:16]; memCurrent_byte3[7:0] = dataOut[31:24]; memIn_byte0[7:0] = memIn[7:0];
  //   memIn_byte1[7:0] = memIn[15:8]; memIn_byte2[7:0] = memIn[23:16]; memIn_byte3[7:0] = memIn[31:24]

  // Notes on the sheet:
  //   Inputs
  //   RAM (note: this does not behave like real memory)
  //   Determine which bytes to keep and which to overwrite
  //   Leave load input floating, so data is always outputed
  //   Outputs
endmodule

module memoryController (
  input  [31:0] addressIn,
  input  [31:0] dataWriteIn,
  input  [1:0] length,
  input  storeIn,
  input  loadIn,
  input  loadUnsigned,
  input  [31:0] memoryOut,
  input  clk,
  input  reset,
  output [31:0] memAddress,
  output [31:0] memDataIn,
  output [3:0] byteSelect,
  output storeOut,
  output loadOut,
  output [31:0] readOut
);

  wire and_1_out, and_2_out, and_3_out, and_4_out, and_11_out, and_12_out, and_13_out, and_16_out,
       and_17_out, and_21_out, and_22_out, and_23_out, comparator_2_eq, comparator_3_eq, comparator_4_gt,
       comparator_5_eq, comparator_6_eq, comparator_7_eq, comparator_8_eq, comparator_9_eq, comparator_10_eq,
       comparator_11_eq, comparator_12_eq, comparator_14_eq, comparator_15_eq, comparator_16_eq,
       comparator_17_eq, comparator_18_eq, comparator_20_eq, comparator_21_gt, comparator_23_eq,
       comparator_24_eq, comparator_25_eq, comparator_26_lt, comparator_27_eq, comparator_28_eq,
       comparator_29_eq, comparator_30_eq, comparator_31_eq, comparator_32_eq, comparator_33_eq,
       comparator_34_eq, comparator_35_eq, comparator_36_eq, comparator_37_eq, comparator_38_eq,
       comparator_39_eq, comparator_40_eq, loadUnsigned_t, m1_b0Select, m1_b1Select, m2_b0Select,
       m2_b2Select, m3_b0Select, m3_b1Select, m3_b3Select, nand_1_out, nor_1_out, nor_2_out, nor_3_out,
       not_1_out, or_1_out;
  wire [1:0] length_t, priority_encoder_1_out, priority_encoder_2_out, priority_encoder_3_out,
       priority_encoder_4_out;
  wire [7:7] and_9_out, and_10_out, and_14_out, and_15_out, and_18_out, and_19_out, and_20_out;
  wire [31:0] dataIn;

  // Probe on memoryOut
  or or_1 (or_1_out, storeIn, loadIn, reset);
  _32b_latch u_32b_latch_1 (.D(addressIn), .CLK(or_1_out), .Q(memAddress));
  _32b_latch u_32b_latch_2 (.D(dataWriteIn), .CLK(or_1_out), .Q(dataIn));
  _2b_latch u_2b_latch_1 (.D(length), .CLK(or_1_out), .Q(length_t));
  D_Latch d_latch_1 (.D(loadUnsigned), .CLK(or_1_out), .Q(loadUnsigned_t));
  Comparator #(.width(2), .mode("unsigned")) comparator_1 (
    .a(memAddress[1:0]), .b(2'b00), .eq(byteSelect[0]));  // open: gt, lt
  Comparator #(.width(2), .mode("unsigned")) comparator_2 (
    .a(memAddress[1:0]), .b(2'b01), .eq(comparator_2_eq));  // open: gt, lt
  Comparator #(.width(2), .mode("unsigned")) comparator_3 (
    .a(memAddress[1:0]), .b(2'b00), .eq(comparator_3_eq));  // open: gt, lt
  Comparator #(.width(2), .mode("unsigned")) comparator_4 (
    .a(length_t), .b(2'b00), .gt(comparator_4_gt));  // open: eq, lt
  Comparator #(.width(2), .mode("unsigned")) comparator_5 (
    .a(memAddress[1:0]), .b(2'b10), .eq(comparator_5_eq));  // open: gt, lt
  Comparator #(.width(2), .mode("unsigned")) comparator_6 (
    .a(memAddress[1:0]), .b(2'b00), .eq(comparator_6_eq));  // open: gt, lt
  Comparator #(.width(2), .mode("unsigned")) comparator_7 (
    .a(length_t), .b(2'b11), .eq(comparator_7_eq));  // open: gt, lt
  Comparator #(.width(2), .mode("unsigned")) comparator_8 (
    .a(memAddress[1:0]), .b(2'b11), .eq(comparator_8_eq));  // open: gt, lt
  Comparator #(.width(2), .mode("unsigned")) comparator_9 (
    .a(memAddress[1:0]), .b(2'b10), .eq(comparator_9_eq));  // open: gt, lt
  Comparator #(.width(2), .mode("unsigned")) comparator_10 (
    .a(length_t), .b(2'b01), .eq(comparator_10_eq));  // open: gt, lt
  Comparator #(.width(2), .mode("unsigned")) comparator_11 (
    .a(memAddress[1:0]), .b(2'b00), .eq(comparator_11_eq));  // open: gt, lt
  Comparator #(.width(2), .mode("unsigned")) comparator_12 (
    .a(length_t), .b(2'b11), .eq(comparator_12_eq));  // open: gt, lt
  and and_1 (and_1_out, comparator_3_eq, comparator_4_gt);
  and and_2 (and_2_out, comparator_6_eq, comparator_7_eq);
  and and_3 (and_3_out, comparator_9_eq, comparator_10_eq);
  and and_4 (and_4_out, comparator_11_eq, comparator_12_eq);
  or or_2 (byteSelect[1], comparator_2_eq, and_1_out);
  or or_3 (byteSelect[2], comparator_5_eq, and_2_out);
  or or_4 (byteSelect[3], comparator_8_eq, and_3_out, and_4_out);
  Comparator #(.width(2), .mode("unsigned")) comparator_13 (
    .a(memAddress[1:0]), .b(2'b11), .eq(m3_b0Select));  // open: gt, lt
  Comparator #(.width(2), .mode("unsigned")) comparator_14 (
    .a(memAddress[1:0]), .b(2'b10), .eq(comparator_14_eq));  // open: gt, lt
  Comparator #(.width(2), .mode("unsigned")) comparator_15 (
    .a(length_t), .b(2'b01), .eq(comparator_15_eq));  // open: gt, lt
  Comparator #(.width(2), .mode("unsigned")) comparator_16 (
    .a(memAddress[1:0]), .b(2'b00), .eq(comparator_16_eq));  // open: gt, lt
  Comparator #(.width(2), .mode("unsigned")) comparator_17 (
    .a(length_t), .b(2'b11), .eq(comparator_17_eq));  // open: gt, lt
  and and_5 (m3_b1Select, comparator_14_eq, comparator_15_eq);
  and and_6 (m3_b3Select, comparator_16_eq, comparator_17_eq);
  Multiplexer #(.width(8), .enable("false")) multiplexer_1 (
    .in0({8{1'b0}}), .in1(dataIn[7:0]), .out(memDataIn[7:0]), .sel(comparator_18_eq));
  Comparator #(.width(2), .mode("unsigned")) comparator_18 (
    .a(memAddress[1:0]), .b(2'b00), .eq(comparator_18_eq));  // open: gt, lt
  Multiplexer #(.select(2), .width(8), .enable("false")) multiplexer_2 (
    .in0({8{1'b0}}), .in1(dataIn[7:0]), .in2(dataIn[15:8]), .out(memDataIn[15:8]),
    .sel({m1_b1Select, m1_b0Select}));  // open: in3
  Comparator #(.width(2), .mode("unsigned")) comparator_19 (
    .a(memAddress[1:0]), .b(2'b01), .eq(m1_b0Select));  // open: gt, lt
  Comparator #(.width(2), .mode("unsigned")) comparator_20 (
    .a(memAddress[1:0]), .b(2'b00), .eq(comparator_20_eq));  // open: gt, lt
  Comparator #(.width(2), .mode("unsigned")) comparator_21 (
    .a(length_t), .b(2'b00), .gt(comparator_21_gt));  // open: eq, lt
  Multiplexer #(.select(2), .width(8), .enable("false")) multiplexer_3 (
    .in0({8{1'b0}}), .in1(dataIn[7:0]), .in2(dataIn[23:16]), .out(memDataIn[23:16]),
    .sel({m2_b2Select, m2_b0Select}));  // open: in3
  Comparator #(.width(2), .mode("unsigned")) comparator_22 (
    .a(memAddress[1:0]), .b(2'b10), .eq(m2_b0Select));  // open: gt, lt
  Comparator #(.width(2), .mode("unsigned")) comparator_23 (
    .a(memAddress[1:0]), .b(2'b00), .eq(comparator_23_eq));  // open: gt, lt
  Comparator #(.width(2), .mode("unsigned")) comparator_24 (
    .a(length_t), .b(2'b11), .eq(comparator_24_eq));  // open: gt, lt
  Multiplexer #(.select(2), .width(8), .enable("false")) multiplexer_4 (
    .in0({8{1'b0}}), .in1(dataIn[7:0]), .in2(dataIn[15:8]), .in3(dataIn[31:24]), .out(memDataIn[31:24]),
    .sel(priority_encoder_1_out));
  and and_7 (m1_b1Select, comparator_20_eq, comparator_21_gt);
  and and_8 (m2_b2Select, comparator_23_eq, comparator_24_eq);
  nand nand_1 (nand_1_out, m3_b0Select, m3_b1Select, m3_b3Select);
  Priority_Encoder #(.select(2)) priority_encoder_1 (
    .in0(nand_1_out), .in1(m3_b0Select), .in2(m3_b1Select), .in3(m3_b3Select), .out(priority_encoder_1_out),
    .en_in(1'b1));  // open: gs, en_out
  Comparator #(.width(2), .mode("unsigned")) comparator_25 (
    .a(memAddress[1:0]), .b(2'b00), .eq(comparator_25_eq));  // open: gt, lt
  Comparator #(.width(2), .mode("unsigned")) comparator_26 (
    .a(length_t), .b(2'b01), .lt(comparator_26_lt));  // open: gt, eq
  not not_1 (not_1_out, comparator_26_lt);
  Comparator #(.width(2), .mode("unsigned")) comparator_27 (
    .a(memAddress[1:0]), .b(2'b10), .eq(comparator_27_eq));  // open: gt, lt
  Comparator #(.width(2), .mode("unsigned")) comparator_28 (
    .a(length_t), .b(2'b01), .eq(comparator_28_eq));  // open: gt, lt
  Comparator #(.width(2), .mode("unsigned")) comparator_29 (
    .a(memAddress[1:0]), .b(2'b10), .eq(comparator_29_eq));  // open: gt, lt
  Comparator #(.width(2), .mode("unsigned")) comparator_30 (
    .a(length_t), .b(2'b00), .eq(comparator_30_eq));  // open: gt, lt
  Comparator #(.width(2), .mode("unsigned")) comparator_31 (
    .a(memAddress[1:0]), .b(2'b00), .eq(comparator_31_eq));  // open: gt, lt
  Comparator #(.width(2), .mode("unsigned")) comparator_32 (
    .a(length_t), .b(2'b11), .eq(comparator_32_eq));  // open: gt, lt
  Comparator #(.width(2), .mode("unsigned")) comparator_33 (
    .a(memAddress[1:0]), .b(2'b00), .eq(comparator_33_eq));  // open: gt, lt
  Comparator #(.width(2), .mode("unsigned")) comparator_34 (
    .a(length_t), .b(2'b01), .eq(comparator_34_eq));  // open: gt, lt
  Comparator #(.width(2), .mode("unsigned")) comparator_35 (
    .a(memAddress[1:0]), .b(2'b00), .eq(comparator_35_eq));  // open: gt, lt
  Comparator #(.width(2), .mode("unsigned")) comparator_36 (
    .a(length_t), .b(2'b11), .eq(comparator_36_eq));  // open: gt, lt
  Comparator #(.width(2), .mode("unsigned")) comparator_37 (
    .a(memAddress[1:0]), .b(2'b00), .eq(comparator_37_eq));  // open: gt, lt
  Comparator #(.width(2), .mode("unsigned")) comparator_38 (
    .a(length_t), .b(2'b01), .eq(comparator_38_eq));  // open: gt, lt
  Comparator #(.width(2), .mode("unsigned")) comparator_39 (
    .a(memAddress[1:0]), .b(2'b10), .eq(comparator_39_eq));  // open: gt, lt
  Comparator #(.width(2), .mode("unsigned")) comparator_40 (
    .a(length_t), .b(2'b01), .eq(comparator_40_eq));  // open: gt, lt
  and and_9 (and_9_out[7], ~loadUnsigned_t, memoryOut[7]);  // AND_Gate
  and and_10 (and_10_out[7], ~loadUnsigned_t, memoryOut[23]);  // AND_Gate
  and and_11 (and_11_out, comparator_25_eq, not_1_out);
  and and_12 (and_12_out, comparator_27_eq, comparator_28_eq);
  and and_13 (and_13_out, comparator_29_eq, comparator_30_eq);
  and and_14 (and_14_out[7], ~loadUnsigned_t, memoryOut[7]);  // AND_Gate
  and and_15 (and_15_out[7], ~loadUnsigned_t, memoryOut[15]);  // AND_Gate
  and and_16 (and_16_out, comparator_31_eq, comparator_32_eq);
  and and_17 (and_17_out, comparator_33_eq, comparator_34_eq);
  and and_18 (and_18_out[7], ~loadUnsigned_t, memoryOut[7]);  // AND_Gate
  and and_19 (and_19_out[7], ~loadUnsigned_t, memoryOut[15]);  // AND_Gate
  and and_20 (and_20_out[7], ~loadUnsigned_t, memoryOut[23]);  // AND_Gate
  and and_21 (and_21_out, comparator_35_eq, comparator_36_eq);
  and and_22 (and_22_out, comparator_37_eq, comparator_38_eq);
  and and_23 (and_23_out, comparator_39_eq, comparator_40_eq);
  nor nor_1 (nor_1_out, and_11_out, and_12_out, and_13_out);
  nor nor_2 (nor_2_out, and_16_out, and_17_out);
  nor nor_3 (nor_3_out, and_21_out, and_22_out, and_23_out);
  Multiplexer #(.select(2), .width(8), .enable("false")) multiplexer_5 (
    .in0(memoryOut[7:0]), .in1(memoryOut[15:8]), .in2(memoryOut[23:16]), .in3(memoryOut[31:24]),
    .out(readOut[7:0]), .sel(memAddress[1:0]));
  Multiplexer #(.select(2), .width(8), .enable("false")) multiplexer_6 (
    .in0(memoryOut[15:8]), .in1({8{and_9_out[7]}}), .in2(memoryOut[31:24]), .in3({8{and_10_out[7]}}),
    .out(readOut[15:8]), .sel(priority_encoder_2_out));
  Priority_Encoder #(.select(2)) priority_encoder_2 (
    .in0(and_11_out), .in1(nor_1_out), .in2(and_12_out), .in3(and_13_out), .out(priority_encoder_2_out),
    .en_in(1'b1));  // open: gs, en_out
  Multiplexer #(.select(2), .width(8), .enable("false")) multiplexer_7 (
    .in0(memoryOut[23:16]), .in1({8{and_14_out[7]}}), .in2({8{and_15_out[7]}}), .out(readOut[23:16]),
    .sel(priority_encoder_3_out));  // open: in3
  Priority_Encoder #(.select(2)) priority_encoder_3 (
    .in0(and_16_out), .in1(nor_2_out), .in2(and_17_out), .in3(1'b0), .out(priority_encoder_3_out),
    .en_in(1'b1));  // open: gs, en_out
  Multiplexer #(.select(2), .width(8), .enable("false")) multiplexer_8 (
    .in0(memoryOut[31:24]), .in1({8{and_18_out[7]}}), .in2({8{and_19_out[7]}}), .in3({8{and_20_out[7]}}),
    .out(readOut[31:24]), .sel(priority_encoder_4_out));
  Priority_Encoder #(.select(2)) priority_encoder_4 (
    .in0(and_21_out), .in1(nor_3_out), .in2(and_22_out), .in3(and_23_out), .out(priority_encoder_4_out),
    .en_in(1'b1));  // open: gs, en_out
  // Probe on readOut

  assign loadOut = loadIn;
  assign storeOut = storeIn;

  // Other names for the same wires on the sheet: address[31:0] = memAddress; addressLower[1:0] = memAddress[1:0];
  //   B0_write = byteSelect[0]; B1_write = byteSelect[1]; B2_write = byteSelect[2]; B3_write = byteSelect[3];
  //   input_byte0[7:0] = dataIn[7:0]; input_byte1[7:0] = dataIn[15:8]; input_byte2[7:0] = dataIn[23:16];
  //   input_byte3[7:0] = dataIn[31:24]; dataReadOut[31:0] = readOut; readOut_byte0[7:0] = readOut[7:0];
  //   readOut_byte1[7:0] = readOut[15:8]; readOut_byte2[7:0] = readOut[23:16]; readOut_byte3[7:0] = readOut[31:24];
  //   load = loadIn; memIn_byte0[7:0] = memDataIn[7:0]; memIn_byte1[7:0] = memDataIn[15:8];
  //   memIn_byte2[7:0] = memDataIn[23:16]; memIn_byte3[7:0] = memDataIn[31:24]; memReadOut[31:0] = memoryOut;
  //   read_byte0[7:0] = memoryOut[7:0]; read_byte1[7:0] = memoryOut[15:8]; read_byte2[7:0] = memoryOut[23:16];
  //   read_byte3[7:0] = memoryOut[31:24]; store = storeIn

  // Notes on the sheet:
  //   Inputs
  //   Input Buffers
  //   Determine which bytes to write
  //   Rearrange data based on length and address
  //   Sign extend read data based on length
  //   Outputs
endmodule

module D_Latch (
  input  D,
  input  CLK,
  output Q
);

  wire nand_1_out, nand_2_out, nand_4_out;

  nand nand_1 (nand_1_out, D, CLK);
  nand nand_2 (nand_2_out, nand_1_out, CLK);
  nand nand_3 (Q, nand_1_out, nand_4_out);
  nand nand_4 (nand_4_out, Q, nand_2_out);
endmodule

module _32b_latch (
  input  [31:0] D,
  input  CLK,
  output [31:0] Q
);

  D_Latch d_latch_1 (.D(D[0]), .CLK(CLK), .Q(Q[0]));
  D_Latch d_latch_2 (.D(D[1]), .CLK(CLK), .Q(Q[1]));
  D_Latch d_latch_3 (.D(D[2]), .CLK(CLK), .Q(Q[2]));
  D_Latch d_latch_4 (.D(D[3]), .CLK(CLK), .Q(Q[3]));
  D_Latch d_latch_5 (.D(D[4]), .CLK(CLK), .Q(Q[4]));
  D_Latch d_latch_6 (.D(D[5]), .CLK(CLK), .Q(Q[5]));
  D_Latch d_latch_7 (.D(D[6]), .CLK(CLK), .Q(Q[6]));
  D_Latch d_latch_8 (.D(D[7]), .CLK(CLK), .Q(Q[7]));
  D_Latch d_latch_9 (.D(D[8]), .CLK(CLK), .Q(Q[8]));
  D_Latch d_latch_10 (.D(D[9]), .CLK(CLK), .Q(Q[9]));
  D_Latch d_latch_11 (.D(D[10]), .CLK(CLK), .Q(Q[10]));
  D_Latch d_latch_12 (.D(D[11]), .CLK(CLK), .Q(Q[11]));
  D_Latch d_latch_13 (.D(D[12]), .CLK(CLK), .Q(Q[12]));
  D_Latch d_latch_14 (.D(D[13]), .CLK(CLK), .Q(Q[13]));
  D_Latch d_latch_15 (.D(D[14]), .CLK(CLK), .Q(Q[14]));
  D_Latch d_latch_16 (.D(D[15]), .CLK(CLK), .Q(Q[15]));
  D_Latch d_latch_17 (.D(D[16]), .CLK(CLK), .Q(Q[16]));
  D_Latch d_latch_18 (.D(D[17]), .CLK(CLK), .Q(Q[17]));
  D_Latch d_latch_19 (.D(D[18]), .CLK(CLK), .Q(Q[18]));
  D_Latch d_latch_20 (.D(D[19]), .CLK(CLK), .Q(Q[19]));
  D_Latch d_latch_21 (.D(D[20]), .CLK(CLK), .Q(Q[20]));
  D_Latch d_latch_22 (.D(D[21]), .CLK(CLK), .Q(Q[21]));
  D_Latch d_latch_23 (.D(D[22]), .CLK(CLK), .Q(Q[22]));
  D_Latch d_latch_24 (.D(D[23]), .CLK(CLK), .Q(Q[23]));
  D_Latch d_latch_25 (.D(D[24]), .CLK(CLK), .Q(Q[24]));
  D_Latch d_latch_26 (.D(D[25]), .CLK(CLK), .Q(Q[25]));
  D_Latch d_latch_27 (.D(D[26]), .CLK(CLK), .Q(Q[26]));
  D_Latch d_latch_28 (.D(D[27]), .CLK(CLK), .Q(Q[27]));
  D_Latch d_latch_29 (.D(D[28]), .CLK(CLK), .Q(Q[28]));
  D_Latch d_latch_30 (.D(D[29]), .CLK(CLK), .Q(Q[29]));
  D_Latch d_latch_31 (.D(D[30]), .CLK(CLK), .Q(Q[30]));
  D_Latch d_latch_32 (.D(D[31]), .CLK(CLK), .Q(Q[31]));
endmodule

module _2b_latch (
  input  [1:0] D,
  input  CLK,
  output [1:0] Q
);

  D_Latch d_latch_1 (.D(D[0]), .CLK(CLK), .Q(Q[0]));
  D_Latch d_latch_2 (.D(D[1]), .CLK(CLK), .Q(Q[1]));
endmodule
